// Logisim project DIGITAL_CLOCK_Basic_Function.circ as structural Verilog: 84 circuits, main circuit main
module MakeMomeriesBackToyou (
  input  [7:0] in_1,
  input  [7:0] in_2,
  input  in_3,
  input  [6:0] in_4,
  input  in_5,
  input  [6:0] in_6,
  input  in_7,
  input  in_8,
  input  in_9,
  input  in_10,
  input  [13:0] in_11,
  input  in_12,
  input  [7:0] in_13,
  input  [6:0] in_14,
  input  in_15,
  input  [6:0] in_16,
  input  in_17,
  input  in_18
);

  wire clock_1_out, clock_2_out, clock_3_out, counter9_1_f, mod31_1_f, mod38_1_f;
  wire [3:0] counter_1_q;
  wire [5:0] counter_2_q, counter_3_q;
  wire [13:0] \do , dopro, fa, fapro, la, lapro, mi, mipro, multiplexer_1_out, multiplexer_2_out,
       multiplexer_3_out, re, repro, so, sopro, xi, xipro;

  Buzzer_Do buzzer_do_1 (.M1_Do(\do ));  // open: CLK_8kHz, N1_Do
  Buzzer_Re buzzer_re_1 (.M1_Re(re));  // open: CLK_8kHz, N1_Re
  Buzzer_Mi3 buzzer_mi3_1 (.M1_Mi3(mi));  // open: CLK_8kHz, N1_Mi3
  Buzzer_Fa4 buzzer_fa4_1 (.M1_Fa4(fa));  // open: CLK_8kHz, N1_Fa4
  Buzzer_So5 buzzer_so5_1 (.M1_So5(so));  // open: CLK_8kHz, N1_So5
  Buzzer_La6 buzzer_la6_1 (.M1_La6(la));  // open: CLK_8kHz, N1_La6
  Buzzer_Xi7 buzzer_xi7_1 (.M1_Xi7(xi));  // open: CLK_8kHz, N1_Xi7
  Buzzer_Do_pro buzzer_do_pro_1 (.M1_Do1pro(dopro));  // open: CLK_8kHz, N1_dopro
  Buzzer_Re2_pro buzzer_re2_pro_1 (.M1_Re2pro(repro));  // open: CLK_8kHz, N1_Re2pro
  Buzzer_Mi3pro buzzer_mi3pro_1 (.M1_Mi3(mipro));  // open: CLK_8kHz, N1_Mi3
  Buzzer_Fa4_pro buzzer_fa4_pro_1 (.M1_Fa4pro(fapro));  // open: CLK_8kHz, N1_Fa4pro
  Buzzer_So5_pro buzzer_so5_pro_1 (.M1_So5pro(sopro));  // open: CLK_8kHz, N1_So5pro
  Buzzer_La6_pro buzzer_la6_pro_1 (.M1_La6pro(lapro));  // open: CLK_8kHz, N1_La6pro
  Buzzer_Xi7pro buzzer_xi7pro_1 (.M1_Xi7(xipro));  // open: CLK_8kHz, N1_Xi7
  Multiplexer #(.select(4), .width(14)) multiplexer_1 (
    .out(multiplexer_1_out), .sel(counter_1_q));  // open: in0, in1, in2, in3, in4, in5, in6, in7, in8, in9, in10, in11, in12, in13, in14, in15
  Multiplexer #(.select(6), .width(14)) multiplexer_2 (
    .in0({14{1'b0}}), .in1(dopro), .in2(repro), .in3(mipro), .in4(sopro), .in5(dopro), .in6(repro),
    .in7(repro), .in8({14{1'b0}}), .in9({14{1'b0}}), .in10(xi), .in11(la), .in12(so), .in13(so), .in14(so),
    .in15(repro), .in16(dopro), .in17(dopro), .in18({14{1'b0}}), .in19({14{1'b0}}), .in20(dopro),
    .in21(repro), .in22(mipro), .in23(sopro), .in24(sopro), .in25(dopro), .in26(repro), .in27(repro),
    .in28({14{1'b0}}), .in29({14{1'b0}}), .in30(repro), .in31(mipro), .in32(lapro), .in33(sopro),
    .in34(mipro), .in35(sopro), .in36(sopro), .in37({14{1'b0}}), .in38({14{1'b0}}), .out(multiplexer_2_out),
    .sel(counter_2_q));  // open: in39, in40, in41, in42, in43, in44, in45, in46, in47, in48, in49, in50, in51, in52, in53, in54, in55, in56, in57, in58, in59, in60, in61, in62, in63
  Counter #(.max('hf), .width(4)) counter_1 (
    .clr(counter9_1_f), .load(in_17), .up(in_18), .count(in_18), .clk(clock_1_out), .Q(counter_1_q));  // open: D, carry
  Clock clock_1 (.out(clock_1_out));
  Counter #(.max('h3f), .width(6)) counter_2 (
    .clr(mod38_1_f), .load(in_9), .up(in_10), .count(in_10), .clk(clock_2_out), .Q(counter_2_q));  // open: D, carry
  Clock clock_2 (.out(clock_2_out));
  // Buzzer buzzer_1: pin names not known; wires that end beside it: in_13, multiplexer_1_out, in_15, in_16
  // Buzzer #(.smooth_level(8), .smooth_width(9), .waveform("Triangle")) buzzer_2: pin names not known; wires that end beside it: dopro, repro, in_2, multiplexer_2_out, in_5, in_6
  // BCD_to_7_Segment_decoder bcd_to_7_segment_decoder_1: pin names not known
  _7_Segment_Display u_7_segment_display_1 ();  // open: g, f, a, b, e, d, c, dp
  // Binary_to_BCD_converter #(.binvalue(4)) binary_to_bcd_converter_1: pin names not known; wires that end beside it: counter_1_q
  // BCD_to_7_Segment_decoder bcd_to_7_segment_decoder_2: pin names not known
  _7_Segment_Display u_7_segment_display_2 ();  // open: g, f, a, b, e, d, c, dp
  // BCD_to_7_Segment_decoder bcd_to_7_segment_decoder_3: pin names not known
  _7_Segment_Display u_7_segment_display_3 ();  // open: g, f, a, b, e, d, c, dp
  // Binary_to_BCD_converter #(.binvalue(6)) binary_to_bcd_converter_2: pin names not known; wires that end beside it: counter_2_q
  Counter9 counter9_1 (.A(counter_1_q), .F(counter9_1_f));
  // BCD_to_7_Segment_decoder bcd_to_7_segment_decoder_4: pin names not known
  _7_Segment_Display u_7_segment_display_4 ();  // open: g, f, a, b, e, d, c, dp
  // Buzzer buzzer_3: pin names not known; wires that end beside it: in_11, in_12, in_14
  MOD38 mod38_1 (.A(counter_2_q), .F(mod38_1_f));
  Multiplexer #(.select(6), .width(14)) multiplexer_3 (
    .out(multiplexer_3_out), .sel(counter_3_q));  // open: in0, in1, in2, in3, in4, in5, in6, in7, in8, in9, in10, in11, in12, in13, in14, in15, in16, in17, in18, in19, in20, in21, in22, in23, in24, in25, in26, in27, in28, in29, in30, in31, in32, in33, in34, in35, in36, in37, in38, in39, in40, in41, in42, in43, in44, in45, in46, in47, in48, in49, in50, in51, in52, in53, in54, in55, in56, in57, in58, in59, in60, in61, in62, in63
  Counter #(.max('h3f), .width(6)) counter_3 (
    .clr(mod31_1_f), .load(in_7), .up(in_8), .count(in_8), .clk(clock_3_out), .Q(counter_3_q));  // open: D, carry
  Clock clock_3 (.out(clock_3_out));
  // Buzzer #(.smooth_width(5)) buzzer_4: pin names not known; wires that end beside it: in_1, multiplexer_3_out, in_3, in_4
  // BCD_to_7_Segment_decoder bcd_to_7_segment_decoder_5: pin names not known
  _7_Segment_Display u_7_segment_display_5 ();  // open: g, f, a, b, e, d, c, dp
  // Binary_to_BCD_converter #(.binvalue(6)) binary_to_bcd_converter_3: pin names not known; wires that end beside it: counter_3_q
  // BCD_to_7_Segment_decoder bcd_to_7_segment_decoder_6: pin names not known
  _7_Segment_Display u_7_segment_display_6 ();  // open: g, f, a, b, e, d, c, dp
  MOD31 mod31_1 (.A(counter_3_q), .F(mod31_1_f));
endmodule

module main (
  input  SET_HOUR,
  input  in_2,
  input  ENABLE_HOUR,
  input  [4:0] SETVAL_HOUR,
  input  SET_MINUTE,
  input  in_6,
  input  ENABLE_MINUTE,
  input  [5:0] SETVAL_MINUTE,
  input  SET_Second,
  input  in_10,
  input  ENABLE_Second,
  input  [5:0] SETVAL_Second,
  output [4:0] OUTVAL_HOUR,
  output ACC_HOUR,
  output [5:0] OUTVAL_MINUTE,
  output [5:0] OUTVAL_Second
);

  wire CLOCK_Second_out, counter60_1_f1, counter60_2_f1;

  Clock CLOCK_Second (.out(CLOCK_Second_out));
  Counter #(.max('h1f), .width(5)) counter_1 (
    .clr(ACC_HOUR), .load(SET_HOUR), .up(in_2), .count(ENABLE_HOUR), .clk(counter60_1_f1), .D(SETVAL_HOUR),
    .Q(OUTVAL_HOUR));  // open: carry
  Counter #(.max('h3f), .width(6)) counter_2 (
    .clr(counter60_1_f1), .load(SET_MINUTE), .up(in_6), .count(ENABLE_MINUTE), .clk(counter60_2_f1),
    .D(SETVAL_MINUTE), .Q(OUTVAL_MINUTE));  // open: carry
  Counter #(.max('h3f), .width(6)) counter_3 (
    .clr(counter60_2_f1), .load(SET_Second), .up(in_10), .count(ENABLE_Second), .clk(CLOCK_Second_out),
    .D(SETVAL_Second), .Q(OUTVAL_Second));  // open: carry
  Counter24 counter24_1 (.Counter24(OUTVAL_HOUR), .F2(ACC_HOUR));
  Counter60 counter60_1 (.Counter60(OUTVAL_MINUTE), .F1(counter60_1_f1));
  Counter60 counter60_2 (.Counter60(OUTVAL_Second), .F1(counter60_2_f1));
  // BCD_to_7_Segment_decoder bcd_to_7_segment_decoder_1: pin names not known
  _7_Segment_Display u_7_segment_display_1 ();  // open: g, f, a, b, e, d, c, dp
  // Binary_to_BCD_converter #(.binvalue(5)) binary_to_bcd_converter_1: pin names not known; wires that end beside it: OUTVAL_HOUR
  // BCD_to_7_Segment_decoder bcd_to_7_segment_decoder_2: pin names not known
  _7_Segment_Display u_7_segment_display_2 ();  // open: g, f, a, b, e, d, c, dp
  // BCD_to_7_Segment_decoder bcd_to_7_segment_decoder_3: pin names not known
  _7_Segment_Display u_7_segment_display_3 ();  // open: g, f, a, b, e, d, c, dp
  // Binary_to_BCD_converter #(.binvalue(6)) binary_to_bcd_converter_2: pin names not known; wires that end beside it: OUTVAL_MINUTE
  // BCD_to_7_Segment_decoder bcd_to_7_segment_decoder_4: pin names not known
  _7_Segment_Display u_7_segment_display_4 ();  // open: g, f, a, b, e, d, c, dp
  // BCD_to_7_Segment_decoder bcd_to_7_segment_decoder_5: pin names not known
  // BCD_to_7_Segment_decoder bcd_to_7_segment_decoder_6: pin names not known
  _7_Segment_Display u_7_segment_display_5 ();  // open: g, f, a, b, e, d, c, dp
  _7_Segment_Display u_7_segment_display_6 ();  // open: g, f, a, b, e, d, c, dp
  // Binary_to_BCD_converter #(.binvalue(6)) binary_to_bcd_converter_3: pin names not known; wires that end beside it: OUTVAL_Second
endmodule

module DigitClock (
  input  SET_HOUR,
  input  SET_Second,
  input  [4:0] SETVAL_HOUR,
  input  [5:0] SETVAL_Second,
  input  ENABLE_ALL,
  input  SET_1,
  input  SET_MINUTE,
  input  [5:0] SETVAL_MINUTE,
  output [4:0] OUTVAL_HOUR,
  output [5:0] OUTVAL_Second,
  output ACC_HOUR,
  output [5:0] OUTVAL_MINUTE
);

  wire binary_to_bcd_converter_1_p2, binary_to_bcd_converter_1_p3, binary_to_bcd_converter_2_p2,
       binary_to_bcd_converter_2_p3, CLOCK_Second_out, counter60_1_f1, counter60_2_f1,
       n7_segment_display_1_p1, n7_segment_display_1_p2;

  Clock CLOCK_Second (.out(CLOCK_Second_out));
  Counter #(.max('h3f), .width(6)) counter_1 (
    .clr(counter60_1_f1), .load(SET_Second), .up(ENABLE_ALL), .count(ENABLE_ALL), .clk(CLOCK_Second_out),
    .D(SETVAL_Second), .Q(OUTVAL_Second));  // open: carry
  Counter #(.max('h3f), .width(6)) counter_2 (
    .clr(counter60_2_f1), .load(SET_MINUTE), .up(ENABLE_ALL), .count(ENABLE_ALL), .clk(counter60_1_f1),
    .D(SETVAL_MINUTE), .Q(OUTVAL_MINUTE));  // open: carry
  // Binary_to_BCD_converter #(.binvalue(6)) binary_to_bcd_converter_1: pin names not known; wires that end beside it: OUTVAL_MINUTE, binary_to_bcd_converter_1_p2, binary_to_bcd_converter_1_p3
  // Binary_to_BCD_converter #(.binvalue(6)) binary_to_bcd_converter_2: pin names not known; wires that end beside it: OUTVAL_Second, binary_to_bcd_converter_2_p2, binary_to_bcd_converter_2_p3
  Counter60 counter60_1 (.Counter60(OUTVAL_Second), .F1(counter60_1_f1));
  Counter60 counter60_2 (.Counter60(OUTVAL_MINUTE), .F1(counter60_2_f1));
  // BCD_to_7_Segment_decoder bcd_to_7_segment_decoder_1: pin names not known
  // _7_Segment_Display 7_segment_display_1: pin names not known; wires that end beside it: n7_segment_display_1_p1, n7_segment_display_1_p2
  // BCD_to_7_Segment_decoder bcd_to_7_segment_decoder_2: pin names not known
  // BCD_to_7_Segment_decoder bcd_to_7_segment_decoder_3: pin names not known
  _7_Segment_Display u_7_segment_display_2 ();  // open: g, f, a, b, e, d, c, dp
  // _7_Segment_Display 7_segment_display_3: pin names not known; wires that end beside it: binary_to_bcd_converter_1_p2, binary_to_bcd_converter_1_p3
  // BCD_to_7_Segment_decoder bcd_to_7_segment_decoder_4: pin names not known
  _7_Segment_Display u_7_segment_display_4 ();  // open: g, f, a, b, e, d, c, dp
  Counter #(.max('h1f), .width(5)) counter_3 (
    .clr(ACC_HOUR), .load(SET_HOUR), .up(ENABLE_ALL), .count(ENABLE_ALL), .clk(counter60_2_f1),
    .D(SETVAL_HOUR), .Q(OUTVAL_HOUR));  // open: carry
  // BCD_to_7_Segment_decoder bcd_to_7_segment_decoder_5: pin names not known
  // BCD_to_7_Segment_decoder bcd_to_7_segment_decoder_6: pin names not known
  // _7_Segment_Display 7_segment_display_5: pin names not known; wires that end beside it: binary_to_bcd_converter_2_p2, binary_to_bcd_converter_2_p3
  _7_Segment_Display u_7_segment_display_6 ();  // open: g, f, a, b, e, d, c, dp
  // Binary_to_BCD_converter #(.binvalue(5)) binary_to_bcd_converter_3: pin names not known; wires that end beside it: OUTVAL_HOUR, n7_segment_display_1_p1, n7_segment_display_1_p2
  Counter24 counter24_1 (.Counter24(OUTVAL_HOUR), .F2(ACC_HOUR));

  assign SET_1 = ENABLE_ALL;
endmodule

module Clock_Minute (
  input  SET_MINUTE,
  input  in_2,
  input  ENABLE_MINUTE,
  input  [5:0] SETVAL_MINUTE,
  output [5:0] OUTVAL_MINUTE,
  output ACC_MINUTE
);

  wire CLOCK_MINUTE_out;

  Clock CLOCK_MINUTE (.out(CLOCK_MINUTE_out));
  Counter #(.max('h3f), .width(6)) counter_1 (
    .clr(ACC_MINUTE), .load(SET_MINUTE), .up(in_2), .count(ENABLE_MINUTE), .clk(CLOCK_MINUTE_out),
    .D(SETVAL_MINUTE), .Q(OUTVAL_MINUTE));  // open: carry
  // BCD_to_7_Segment_decoder bcd_to_7_segment_decoder_1: pin names not known
  _7_Segment_Display u_7_segment_display_1 ();  // open: g, f, a, b, e, d, c, dp
  // Binary_to_BCD_converter #(.binvalue(6)) binary_to_bcd_converter_1: pin names not known; wires that end beside it: OUTVAL_MINUTE
  // BCD_to_7_Segment_decoder bcd_to_7_segment_decoder_2: pin names not known
  _7_Segment_Display u_7_segment_display_2 ();  // open: g, f, a, b, e, d, c, dp
  Counter60 counter60_1 (.Counter60(OUTVAL_MINUTE), .F1(ACC_MINUTE));
endmodule

module Clock_Adjusted (
  input  SET_HOUR,
  input  in_2,
  input  ENABLE_HOUR,
  input  [4:0] SETVAL_HOUR,
  input  SET_MINUTE,
  input  in_6,
  input  ENABLE_MINUTE,
  input  [5:0] SETVAL_MINUTE,
  input  SET_Second,
  input  in_10,
  input  ENABLE_Second,
  input  [5:0] SETVAL_Second,
  output [4:0] OUTVAL_HOUR,
  output ACC_HOUR,
  output [5:0] OUTVAL_MINUTE,
  output [5:0] OUTVAL_Second
);

  wire ADDButtun_Hour_out, ADDButtun_Minute_out, ADDButtun_Second_out, CLOCK_Second_out, counter60_1_f1,
       counter60_2_f1, or_1_out, or_2_out, or_3_out;

  Button ADDButtun_Hour (.out(ADDButtun_Hour_out));
  Button ADDButtun_Minute (.out(ADDButtun_Minute_out));
  Clock CLOCK_Second (.out(CLOCK_Second_out));
  or or_1 (or_1_out, ADDButtun_Hour_out, counter60_1_f1);
  Button ADDButtun_Second (.out(ADDButtun_Second_out));
  or or_2 (or_2_out, ADDButtun_Minute_out, counter60_2_f1);
  or or_3 (or_3_out, CLOCK_Second_out, ADDButtun_Second_out);
  Counter #(.max('h1f), .width(5)) counter_1 (
    .clr(ACC_HOUR), .load(SET_HOUR), .up(in_2), .count(ENABLE_HOUR), .clk(or_1_out), .D(SETVAL_HOUR),
    .Q(OUTVAL_HOUR));  // open: carry
  Counter #(.max('h3f), .width(6)) counter_2 (
    .clr(counter60_1_f1), .load(SET_MINUTE), .up(in_6), .count(ENABLE_MINUTE), .clk(or_2_out),
    .D(SETVAL_MINUTE), .Q(OUTVAL_MINUTE));  // open: carry
  Counter #(.max('h3f), .width(6)) counter_3 (
    .clr(counter60_2_f1), .load(SET_Second), .up(in_10), .count(ENABLE_Second), .clk(or_3_out),
    .D(SETVAL_Second), .Q(OUTVAL_Second));  // open: carry
  Counter24 counter24_1 (.Counter24(OUTVAL_HOUR), .F2(ACC_HOUR));
  Counter60 counter60_1 (.Counter60(OUTVAL_MINUTE), .F1(counter60_1_f1));
  Counter60 counter60_2 (.Counter60(OUTVAL_Second), .F1(counter60_2_f1));
  // BCD_to_7_Segment_decoder bcd_to_7_segment_decoder_1: pin names not known
  _7_Segment_Display u_7_segment_display_1 ();  // open: g, f, a, b, e, d, c, dp
  // Binary_to_BCD_converter #(.binvalue(5)) binary_to_bcd_converter_1: pin names not known; wires that end beside it: OUTVAL_HOUR
  // BCD_to_7_Segment_decoder bcd_to_7_segment_decoder_2: pin names not known
  _7_Segment_Display u_7_segment_display_2 ();  // open: g, f, a, b, e, d, c, dp
  // BCD_to_7_Segment_decoder bcd_to_7_segment_decoder_3: pin names not known
  _7_Segment_Display u_7_segment_display_3 ();  // open: g, f, a, b, e, d, c, dp
  // Binary_to_BCD_converter #(.binvalue(6)) binary_to_bcd_converter_2: pin names not known; wires that end beside it: OUTVAL_MINUTE
  // BCD_to_7_Segment_decoder bcd_to_7_segment_decoder_4: pin names not known
  _7_Segment_Display u_7_segment_display_4 ();  // open: g, f, a, b, e, d, c, dp
  // BCD_to_7_Segment_decoder bcd_to_7_segment_decoder_5: pin names not known
  // BCD_to_7_Segment_decoder bcd_to_7_segment_decoder_6: pin names not known
  _7_Segment_Display u_7_segment_display_5 ();  // open: g, f, a, b, e, d, c, dp
  _7_Segment_Display u_7_segment_display_6 ();  // open: g, f, a, b, e, d, c, dp
  // Binary_to_BCD_converter #(.binvalue(6)) binary_to_bcd_converter_3: pin names not known; wires that end beside it: OUTVAL_Second
endmodule

module Clock_Second (
  input  SET_Second,
  input  in_2,
  input  ENABLE_Second,
  input  [5:0] SETVAL_Second,
  output [5:0] OUTVAL_Second,
  output ACC_Second
);

  wire CLOCK_Second_out;

  Clock CLOCK_Second (.out(CLOCK_Second_out));
  Counter #(.max('h3f), .width(6)) counter_1 (
    .clr(ACC_Second), .load(SET_Second), .up(in_2), .count(ENABLE_Second), .clk(CLOCK_Second_out),
    .D(SETVAL_Second), .Q(OUTVAL_Second));  // open: carry
  // BCD_to_7_Segment_decoder bcd_to_7_segment_decoder_1: pin names not known
  _7_Segment_Display u_7_segment_display_1 ();  // open: g, f, a, b, e, d, c, dp
  // Binary_to_BCD_converter #(.binvalue(6)) binary_to_bcd_converter_1: pin names not known; wires that end beside it: OUTVAL_Second
  // BCD_to_7_Segment_decoder bcd_to_7_segment_decoder_2: pin names not known
  _7_Segment_Display u_7_segment_display_2 ();  // open: g, f, a, b, e, d, c, dp
  Counter60 counter60_1 (.Counter60(OUTVAL_Second), .F1(ACC_Second));
endmodule

module Clock_Hour (
  input  SET_HOUR,
  input  in_2,
  input  ENABLE_HOUR,
  input  [4:0] SETVAL_HOUR,
  output [4:0] OUTVAL_HOUR,
  output ACC_HOUR
);

  wire CLOCK_HOUR_out;

  Clock CLOCK_HOUR (.out(CLOCK_HOUR_out));
  Counter #(.max('h1f), .width(5)) counter_1 (
    .clr(ACC_HOUR), .load(SET_HOUR), .up(in_2), .count(ENABLE_HOUR), .clk(CLOCK_HOUR_out), .D(SETVAL_HOUR),
    .Q(OUTVAL_HOUR));  // open: carry
  // BCD_to_7_Segment_decoder bcd_to_7_segment_decoder_1: pin names not known
  // BCD_to_7_Segment_decoder bcd_to_7_segment_decoder_2: pin names not known
  _7_Segment_Display u_7_segment_display_1 ();  // open: g, f, a, b, e, d, c, dp
  _7_Segment_Display u_7_segment_display_2 ();  // open: g, f, a, b, e, d, c, dp
  // Binary_to_BCD_converter #(.binvalue(5)) binary_to_bcd_converter_1: pin names not known; wires that end beside it: OUTVAL_HOUR
  Counter24 counter24_1 (.Counter24(OUTVAL_HOUR), .F2(ACC_HOUR));
endmodule

module Alarm_fulltime (
  input  SET_HOUR,
  input  in_2,
  input  ENABLE_HOUR,
  input  [4:0] SETVAL_HOUR,
  output [4:0] OUTVAL_HOUR,
  output ACC_HOUR
);

  wire and_1_out, CLOCK_HOUR_out, n7_segment_display_1_p1, n7_segment_display_1_p2, not_1_out;

  Clock CLOCK_HOUR (.out(CLOCK_HOUR_out));
  // BCD_to_7_Segment_decoder bcd_to_7_segment_decoder_1: pin names not known
  // _7_Segment_Display 7_segment_display_1: pin names not known; wires that end beside it: n7_segment_display_1_p1, n7_segment_display_1_p2
  Counter #(.max('h1f), .width(5)) counter_1 (
    .clr(ACC_HOUR), .load(SET_HOUR), .up(in_2), .count(ENABLE_HOUR), .clk(CLOCK_HOUR_out), .D(SETVAL_HOUR),
    .Q(OUTVAL_HOUR));  // open: carry
  // BCD_to_7_Segment_decoder bcd_to_7_segment_decoder_2: pin names not known
  _7_Segment_Display u_7_segment_display_2 ();  // open: g, f, a, b, e, d, c, dp
  // Binary_to_BCD_converter #(.binvalue(5)) binary_to_bcd_converter_1: pin names not known; wires that end beside it: OUTVAL_HOUR, n7_segment_display_1_p1, n7_segment_display_1_p2
  Counter24 counter24_1 (.Counter24(OUTVAL_HOUR), .F2(ACC_HOUR));
  not not_1 (not_1_out, OUTVAL_HOUR[4]);
  and and_1 (and_1_out, OUTVAL_HOUR[0], OUTVAL_HOUR[1], OUTVAL_HOUR[2], OUTVAL_HOUR[3], not_1_out);
  LED led_1 (.in(and_1_out));
endmodule

module Alarm_all (
  input  SET_HOUR,
  input  SET_Second,
  input  [4:0] SETVAL_HOUR,
  input  [5:0] SETVAL_Second,
  input  ENABLE_ALL,
  input  SET_1,
  input  SET_MINUTE,
  input  [5:0] SETVAL_MINUTE,
  output [4:0] OUTVAL_HOUR,
  output [5:0] OUTVAL_Second,
  output ACC_HOUR,
  output [5:0] OUTVAL_MINUTE
);

  wire binary_to_bcd_converter_1_p2, binary_to_bcd_converter_1_p3, binary_to_bcd_converter_2_p2,
       binary_to_bcd_converter_2_p3, CLOCK_Second_out, counter60_1_f1, counter60_2_f1,
       n7_segment_display_1_p1, n7_segment_display_1_p2;

  Clock CLOCK_Second (.out(CLOCK_Second_out));
  // BCD_to_7_Segment_decoder bcd_to_7_segment_decoder_1: pin names not known
  Counter #(.max('h3f), .width(6)) counter_1 (
    .clr(counter60_1_f1), .load(SET_Second), .up(ENABLE_ALL), .count(ENABLE_ALL), .clk(CLOCK_Second_out),
    .D(SETVAL_Second), .Q(OUTVAL_Second));  // open: carry
  Counter #(.max('h3f), .width(6)) counter_2 (
    .clr(counter60_2_f1), .load(SET_MINUTE), .up(ENABLE_ALL), .count(ENABLE_ALL), .clk(counter60_1_f1),
    .D(SETVAL_MINUTE), .Q(OUTVAL_MINUTE));  // open: carry
  // Binary_to_BCD_converter #(.binvalue(6)) binary_to_bcd_converter_1: pin names not known; wires that end beside it: OUTVAL_MINUTE, binary_to_bcd_converter_1_p2, binary_to_bcd_converter_1_p3
  // Binary_to_BCD_converter #(.binvalue(6)) binary_to_bcd_converter_2: pin names not known; wires that end beside it: OUTVAL_Second, binary_to_bcd_converter_2_p2, binary_to_bcd_converter_2_p3
  Counter60 counter60_1 (.Counter60(OUTVAL_Second), .F1(counter60_1_f1));
  Counter60 counter60_2 (.Counter60(OUTVAL_MINUTE), .F1(counter60_2_f1));
  // BCD_to_7_Segment_decoder bcd_to_7_segment_decoder_2: pin names not known
  // _7_Segment_Display 7_segment_display_1: pin names not known; wires that end beside it: n7_segment_display_1_p1, n7_segment_display_1_p2
  // BCD_to_7_Segment_decoder bcd_to_7_segment_decoder_3: pin names not known
  // BCD_to_7_Segment_decoder bcd_to_7_segment_decoder_4: pin names not known
  _7_Segment_Display u_7_segment_display_2 ();  // open: g, f, a, b, e, d, c, dp
  // _7_Segment_Display 7_segment_display_3: pin names not known; wires that end beside it: binary_to_bcd_converter_1_p2, binary_to_bcd_converter_1_p3
  // BCD_to_7_Segment_decoder bcd_to_7_segment_decoder_5: pin names not known
  _7_Segment_Display u_7_segment_display_4 ();  // open: g, f, a, b, e, d, c, dp
  Counter #(.max('h1f), .width(5)) counter_3 (
    .clr(ACC_HOUR), .load(SET_HOUR), .up(ENABLE_ALL), .count(ENABLE_ALL), .clk(counter60_2_f1),
    .D(SETVAL_HOUR), .Q(OUTVAL_HOUR));  // open: carry
  // BCD_to_7_Segment_decoder bcd_to_7_segment_decoder_6: pin names not known
  // BCD_to_7_Segment_decoder bcd_to_7_segment_decoder_7: pin names not known
  // _7_Segment_Display 7_segment_display_5: pin names not known; wires that end beside it: binary_to_bcd_converter_2_p2, binary_to_bcd_converter_2_p3
  _7_Segment_Display u_7_segment_display_6 ();  // open: g, f, a, b, e, d, c, dp
  // Binary_to_BCD_converter #(.binvalue(5)) binary_to_bcd_converter_3: pin names not known; wires that end beside it: OUTVAL_HOUR, n7_segment_display_1_p1, n7_segment_display_1_p2
  Counter24 counter24_1 (.Counter24(OUTVAL_HOUR), .F2(ACC_HOUR));

  assign SET_1 = ENABLE_ALL;
endmodule

module DESIGN_MAIN_3_20 (
  input  SET,
  input  [5:0] SETVAL,
  input  [5:0] TIMEHOUR0,
  input  ENABLREALARM0,
  input  [5:0] TIMEMIN0,
  input  [5:0] TIMESEC0,
  input  in_7,
  input  [5:0] ALARMVAL0,
  input  STOPALARM0,
  input  CLK0,
  input  in_11,
  input  in_12,
  input  SETALARM0,
  input  [2:0] HMSSELECT0,
  output [5:0] ALARMHOUR0,
  output [5:0] ALARMMIN0,
  output [5:0] ALARMSEC0,
  output SETHOUR0,
  output SETMIN0,
  output ACC_HOUR,
  output SETSEC0,
  output ALARMSIG0
);

  wire and_1_out, and_2_out, and_3_out, and_4_out, and_5_out, CLK_out, clock_1_out, comparator_1_eq,
       comparator_2_eq, comparator_3_eq, counter60_1_f1, counter60_2_f1, multiplexer_1_out,
       multiplexer_2_out, or_1_out, or_2_out, or_3_out, TIMESETHOUR, TIMESETMIN, TIMESETSEC;
  wire [5:0] counter_1_q, counter_2_q, counter_3_q, TIMEHOUR, TIMEMIN, TIMESEC;

  Clock clock_1 (.out(clock_1_out));
  Comparator #(.width(6)) comparator_1 (.a(ALARMHOUR0), .b(TIMEHOUR), .eq(comparator_1_eq));  // open: gt, lt
  Comparator #(.width(6)) comparator_2 (.a(ALARMMIN0), .b(TIMEMIN), .eq(comparator_2_eq));  // open: gt, lt
  Comparator #(.width(6)) comparator_3 (.a(ALARMSEC0), .b(TIMESEC), .eq(comparator_3_eq));  // open: gt, lt
  and and_1 (and_1_out, in_7, clock_1_out);
  and and_2 (and_2_out, comparator_1_eq, comparator_2_eq, comparator_3_eq, ENABLREALARM0);
  and and_3 (and_3_out, TIMESETSEC, SET);
  Register #(.width(6)) HOUR (.D(ALARMVAL0), .en(SETHOUR0), .clk(CLK0), .Q(ALARMHOUR0));  // open: clr
  Multiplexer multiplexer_1 (.in0(in_11), .in1(in_12), .out(multiplexer_1_out), .sel(STOPALARM0));
  Clock CLK (.out(CLK_out));
  and and_4 (and_4_out, TIMESETHOUR, SET);
  and and_5 (and_5_out, TIMESETMIN, SET);
  Multiplexer multiplexer_2 (.in0(and_2_out), .in1(CLK_out), .out(multiplexer_2_out), .sel(STOPALARM0));
  Counter #(.max('h3f), .width(6)) counter_1 (
    .clr(ACC_HOUR), .load(SET), .up(in_7), .count(in_7), .clk(or_1_out), .D(SETVAL), .Q(counter_1_q));  // open: carry
  or or_1 (or_1_out, and_4_out, counter60_1_f1);
  or or_2 (or_2_out, and_5_out, counter60_2_f1);
  or or_3 (or_3_out, and_3_out, and_1_out);
  D_Flip_Flop d_ff_1 (.D(multiplexer_1_out), .clk(multiplexer_2_out), .Q(ALARMSIG0));  // open: Qn, preset, reset
  Counter #(.max('h3f), .width(6)) counter_2 (
    .clr(counter60_1_f1), .load(SET), .up(in_7), .count(in_7), .clk(or_2_out), .D(SETVAL), .Q(counter_2_q));  // open: carry
  Counter #(.max('h3f), .width(6)) counter_3 (
    .clr(counter60_2_f1), .load(SET), .up(in_7), .count(in_7), .clk(or_3_out), .D(SETVAL), .Q(counter_3_q));  // open: carry
  assign TIMESEC = counter_3_q;  // OR_Gate or_4, 6 bits wide OR_Gate
  Register #(.width(6)) MIN (.D(ALARMVAL0), .en(SETMIN0), .clk(CLK0), .Q(ALARMMIN0));  // open: clr
  assign TIMEHOUR = counter_1_q;  // OR_Gate or_5, 6 bits wide OR_Gate
  Counter24New counter24new_1 (.Counter24_New(counter_1_q), .F1(ACC_HOUR));
  assign TIMEMIN = counter_2_q;  // OR_Gate or_6, 6 bits wide OR_Gate
  Counter60 counter60_1 (.Counter60(counter_2_q), .F1(counter60_1_f1));
  Counter60 counter60_2 (.Counter60(counter_3_q), .F1(counter60_2_f1));
  Register #(.width(6)) SEC (.D(ALARMVAL0), .en(SETSEC0), .clk(CLK0), .Q(ALARMSEC0));  // open: clr
  Decoder #(.select(3)) decoder_1 (
    .out1(TIMESETHOUR), .out2(TIMESETMIN), .out3(TIMESETSEC), .out5(SETSEC0), .out6(SETHOUR0),
    .out7(SETMIN0), .sel(HMSSELECT0), .en(SETALARM0));  // open: out0, out4
  LED led_1 (.in(TIMESETHOUR));
  // BCD_to_7_Segment_decoder bcd_to_7_segment_decoder_1: pin names not known
  // BCD_to_7_Segment_decoder bcd_to_7_segment_decoder_2: pin names not known
  _7_Segment_Display u_7_segment_display_1 ();  // open: g, f, a, b, e, d, c, dp
  _7_Segment_Display u_7_segment_display_2 ();  // open: g, f, a, b, e, d, c, dp
  // Binary_to_BCD_converter #(.binvalue(6)) binary_to_bcd_converter_1: pin names not known; wires that end beside it: counter_1_q
  // BCD_to_7_Segment_decoder bcd_to_7_segment_decoder_3: pin names not known
  _7_Segment_Display u_7_segment_display_3 ();  // open: g, f, a, b, e, d, c, dp
  // Binary_to_BCD_converter #(.binvalue(6)) binary_to_bcd_converter_2: pin names not known; wires that end beside it: counter_2_q
  LED led_2 (.in(TIMESETMIN));
  // BCD_to_7_Segment_decoder bcd_to_7_segment_decoder_4: pin names not known
  _7_Segment_Display u_7_segment_display_4 ();  // open: g, f, a, b, e, d, c, dp
  // BCD_to_7_Segment_decoder bcd_to_7_segment_decoder_5: pin names not known
  _7_Segment_Display u_7_segment_display_5 ();  // open: g, f, a, b, e, d, c, dp
  // Binary_to_BCD_converter #(.binvalue(6)) binary_to_bcd_converter_3: pin names not known; wires that end beside it: counter_3_q
  LED led_3 (.in(ALARMSIG0));
  LED led_4 (.in(TIMESETSEC));
  // BCD_to_7_Segment_decoder bcd_to_7_segment_decoder_6: pin names not known
  _7_Segment_Display u_7_segment_display_6 ();  // open: g, f, a, b, e, d, c, dp

  // Other names for the same wires on the sheet: ALARMHOUR[5:0] = ALARMHOUR0; ALARMMIN[5:0] = ALARMMIN0;
  //   ALARMSEC[5:0] = ALARMSEC0; ALARMSIG = ALARMSIG0; ALARMVAL[5:0] = ALARMVAL0; CLK = CLK0;
  //   ENABLEALARM = ENABLREALARM0; HMSSELECT[2:0] = HMSSELECT0; SETALARM = SETALARM0; SETHOUR = SETHOUR0;
  //   SETMIN = SETMIN0; SETSEC = SETSEC0; STOPALARM = STOPALARM0
endmodule

module ClockSet_2026_3_13 (
  input  SET_HOUR,
  input  in_2,
  input  [4:0] SETVAL_HOUR,
  input  SET_MINUTE,
  input  [1:0] in_5,
  input  [5:0] SETVAL_MINUTE,
  input  SET_Second,
  input  [5:0] SETVAL_Second,
  input  BEGINandSTOP,
  output [4:0] OUTVAL_HOUR,
  output ACC_HOUR,
  output [5:0] OUTVAL_MINUTE,
  output [5:0] OUTVAL_Second
);

  wire ADDButtun_out, and_1_out, and_2_out, and_3_out, and_4_out, CLOCK_Second_out, counter60_1_f1,
       counter60_2_f1, decoder_1_out1, decoder_1_out2, decoder_1_out3, nor_1_out, or_1_out, or_2_out,
       or_3_out;

  Button ADDButtun (.out(ADDButtun_out));
  Decoder #(.select(2)) decoder_1 (
    .out1(decoder_1_out1), .out2(decoder_1_out2), .out3(decoder_1_out3), .sel(in_5), .en(1'b1));  // open: out0
  and and_1 (and_1_out, decoder_1_out2, ADDButtun_out);
  and and_2 (and_2_out, ADDButtun_out, decoder_1_out1);
  Clock CLOCK_Second (.out(CLOCK_Second_out));
  and and_3 (and_3_out, decoder_1_out3, ADDButtun_out);
  and and_4 (and_4_out, CLOCK_Second_out, BEGINandSTOP);
  nor nor_1 (nor_1_out, and_4_out, and_3_out);
  or or_1 (or_1_out, and_2_out, counter60_1_f1);
  or or_2 (or_2_out, and_1_out, counter60_2_f1);
  or or_3 (or_3_out, nor_1_out, and_3_out);
  Counter #(.max('h1f), .width(5)) counter_1 (
    .clr(ACC_HOUR), .load(SET_HOUR), .up(in_2), .count(in_2), .clk(or_1_out), .D(SETVAL_HOUR), .Q(OUTVAL_HOUR));  // open: carry
  Counter #(.max('h3f), .width(6)) counter_2 (
    .clr(counter60_1_f1), .load(SET_MINUTE), .up(in_2), .count(in_2), .clk(or_2_out), .D(SETVAL_MINUTE),
    .Q(OUTVAL_MINUTE));  // open: carry
  Counter #(.max('h3f), .width(6)) counter_3 (
    .clr(counter60_2_f1), .load(SET_Second), .up(in_2), .count(in_2), .clk(or_3_out), .D(SETVAL_Second),
    .Q(OUTVAL_Second));  // open: carry
  Counter24 counter24_1 (.Counter24(OUTVAL_HOUR), .F2(ACC_HOUR));
  Counter60 counter60_1 (.Counter60(OUTVAL_MINUTE), .F1(counter60_1_f1));
  Counter60 counter60_2 (.Counter60(OUTVAL_Second), .F1(counter60_2_f1));
  // BCD_to_7_Segment_decoder bcd_to_7_segment_decoder_1: pin names not known
  _7_Segment_Display u_7_segment_display_1 ();  // open: g, f, a, b, e, d, c, dp
  // Binary_to_BCD_converter #(.binvalue(5)) binary_to_bcd_converter_1: pin names not known; wires that end beside it: OUTVAL_HOUR
  LED led_1 (.in(decoder_1_out1));
  // BCD_to_7_Segment_decoder bcd_to_7_segment_decoder_2: pin names not known
  _7_Segment_Display u_7_segment_display_2 ();  // open: g, f, a, b, e, d, c, dp
  // BCD_to_7_Segment_decoder bcd_to_7_segment_decoder_3: pin names not known
  // BCD_to_7_Segment_decoder bcd_to_7_segment_decoder_4: pin names not known
  _7_Segment_Display u_7_segment_display_3 ();  // open: g, f, a, b, e, d, c, dp
  _7_Segment_Display u_7_segment_display_4 ();  // open: g, f, a, b, e, d, c, dp
  // Binary_to_BCD_converter #(.binvalue(6)) binary_to_bcd_converter_2: pin names not known; wires that end beside it: OUTVAL_MINUTE
  LED led_2 (.in(decoder_1_out2));
  // BCD_to_7_Segment_decoder bcd_to_7_segment_decoder_5: pin names not known
  _7_Segment_Display u_7_segment_display_5 ();  // open: g, f, a, b, e, d, c, dp
  // Binary_to_BCD_converter #(.binvalue(6)) binary_to_bcd_converter_3: pin names not known; wires that end beside it: OUTVAL_Second
  // BCD_to_7_Segment_decoder bcd_to_7_segment_decoder_6: pin names not known
  _7_Segment_Display u_7_segment_display_6 ();  // open: g, f, a, b, e, d, c, dp
  LED led_3 (.in(decoder_1_out3));
endmodule

module Digital_Clock_Zero (
  input  SET_HOUR,
  input  Input_1,
  input  ENABLE_HOUR,
  input  [4:0] SETVAL_HOUR,
  input  SET_MINUTE,
  input  Input_2,
  input  ENABLE_MINUTE,
  input  [5:0] SETVAL_MINUTE,
  input  SET_Second,
  input  Input_3,
  input  ENABLE_Second,
  input  [5:0] SETVAL_Second,
  output [4:0] OUTVAL_HOUR,
  output ACC_HOUR,
  output [5:0] OUTVAL_MINUTE,
  output [5:0] OUTVAL_Second
);

  wire CLOCK_Second_out, Counter60_1_f1, Counter60_2_f1;

  Clock CLOCK_Second (.out(CLOCK_Second_out));
  Counter #(.max('h1f), .width(5)) counter_1 (
    .clr(ACC_HOUR), .load(SET_HOUR), .up(Input_1), .count(ENABLE_HOUR), .clk(Counter60_1_f1),
    .D(SETVAL_HOUR), .Q(OUTVAL_HOUR));  // open: carry
  Counter #(.max('h3f), .width(6)) counter_2 (
    .clr(Counter60_1_f1), .load(SET_MINUTE), .up(Input_2), .count(ENABLE_MINUTE), .clk(Counter60_2_f1),
    .D(SETVAL_MINUTE), .Q(OUTVAL_MINUTE));  // open: carry
  Counter #(.max('h3f), .width(6)) counter_3 (
    .clr(Counter60_2_f1), .load(SET_Second), .up(Input_3), .count(ENABLE_Second), .clk(CLOCK_Second_out),
    .D(SETVAL_Second), .Q(OUTVAL_Second));  // open: carry
  Counter24 Counter24_1 (.Counter24(OUTVAL_HOUR), .F2(ACC_HOUR));
  Counter60 Counter60_1 (.Counter60(OUTVAL_MINUTE), .F1(Counter60_1_f1));
  Counter60 Counter60_2 (.Counter60(OUTVAL_Second), .F1(Counter60_2_f1));
  // BCD_to_7_Segment_decoder bcd_to_7_segment_decoder_1: pin names not known
  _7_Segment_Display L_7_Segment_Display_1 ();  // open: g, f, a, b, e, d, c, dp
  // Binary_to_BCD_converter #(.binvalue(5)) binary_to_bcd_converter_1: pin names not known; wires that end beside it: OUTVAL_HOUR
  // BCD_to_7_Segment_decoder bcd_to_7_segment_decoder_2: pin names not known
  _7_Segment_Display L_7_Segment_Display_2 ();  // open: g, f, a, b, e, d, c, dp
  // BCD_to_7_Segment_decoder bcd_to_7_segment_decoder_3: pin names not known
  _7_Segment_Display L_7_Segment_Display_3 ();  // open: g, f, a, b, e, d, c, dp
  // Binary_to_BCD_converter #(.binvalue(6)) binary_to_bcd_converter_2: pin names not known; wires that end beside it: OUTVAL_MINUTE
  // BCD_to_7_Segment_decoder bcd_to_7_segment_decoder_4: pin names not known
  _7_Segment_Display L_7_Segment_Display_4 ();  // open: g, f, a, b, e, d, c, dp
  // BCD_to_7_Segment_decoder bcd_to_7_segment_decoder_5: pin names not known
  // BCD_to_7_Segment_decoder bcd_to_7_segment_decoder_6: pin names not known
  _7_Segment_Display L_7_Segment_Display_5 ();  // open: g, f, a, b, e, d, c, dp
  _7_Segment_Display L_7_Segment_Display_6 ();  // open: g, f, a, b, e, d, c, dp
  // Binary_to_BCD_converter #(.binvalue(6)) binary_to_bcd_converter_3: pin names not known; wires that end beside it: OUTVAL_Second
endmodule

module Clock_Set_2026_3_14 (
  input  SET_HOUR,
  input  in_2,
  input  ENABLE_HOUR,
  input  [4:0] SETVAL_HOUR,
  input  SET_MINUTE,
  input  in_6,
  input  ENABLE_MINUTE,
  input  [5:0] SETVAL_MINUTE,
  input  SET_Second,
  input  in_10,
  input  ENABLE_Second,
  input  [5:0] SETVAL_Second,
  output [4:0] OUTVAL_HOUR,
  output ACC_HOUR,
  output [5:0] OUTVAL_MINUTE,
  output [5:0] OUTVAL_Second
);

  wire CLOCK_Second_out, counter60_1_f1, counter60_2_f1;

  Clock CLOCK_Second (.out(CLOCK_Second_out));
  Counter #(.max('h1f), .width(5)) counter_1 (
    .clr(ACC_HOUR), .load(SET_HOUR), .up(in_2), .count(ENABLE_HOUR), .clk(counter60_1_f1), .D(SETVAL_HOUR),
    .Q(OUTVAL_HOUR));  // open: carry
  Counter #(.max('h3f), .width(6)) counter_2 (
    .clr(counter60_1_f1), .load(SET_MINUTE), .up(in_6), .count(ENABLE_MINUTE), .clk(counter60_2_f1),
    .D(SETVAL_MINUTE), .Q(OUTVAL_MINUTE));  // open: carry
  Counter #(.max('h3f), .width(6)) counter_3 (
    .clr(counter60_2_f1), .load(SET_Second), .up(in_10), .count(ENABLE_Second), .clk(CLOCK_Second_out),
    .D(SETVAL_Second), .Q(OUTVAL_Second));  // open: carry
  Counter24 counter24_1 (.Counter24(OUTVAL_HOUR), .F2(ACC_HOUR));
  Counter60 counter60_1 (.Counter60(OUTVAL_MINUTE), .F1(counter60_1_f1));
  Counter60 counter60_2 (.Counter60(OUTVAL_Second), .F1(counter60_2_f1));
  // BCD_to_7_Segment_decoder bcd_to_7_segment_decoder_1: pin names not known
  _7_Segment_Display u_7_segment_display_1 ();  // open: g, f, a, b, e, d, c, dp
  // Binary_to_BCD_converter #(.binvalue(5)) binary_to_bcd_converter_1: pin names not known; wires that end beside it: OUTVAL_HOUR
  // BCD_to_7_Segment_decoder bcd_to_7_segment_decoder_2: pin names not known
  _7_Segment_Display u_7_segment_display_2 ();  // open: g, f, a, b, e, d, c, dp
  // BCD_to_7_Segment_decoder bcd_to_7_segment_decoder_3: pin names not known
  _7_Segment_Display u_7_segment_display_3 ();  // open: g, f, a, b, e, d, c, dp
  // Binary_to_BCD_converter #(.binvalue(6)) binary_to_bcd_converter_2: pin names not known; wires that end beside it: OUTVAL_MINUTE
  // BCD_to_7_Segment_decoder bcd_to_7_segment_decoder_4: pin names not known
  _7_Segment_Display u_7_segment_display_4 ();  // open: g, f, a, b, e, d, c, dp
  // BCD_to_7_Segment_decoder bcd_to_7_segment_decoder_5: pin names not known
  // BCD_to_7_Segment_decoder bcd_to_7_segment_decoder_6: pin names not known
  _7_Segment_Display u_7_segment_display_5 ();  // open: g, f, a, b, e, d, c, dp
  _7_Segment_Display u_7_segment_display_6 ();  // open: g, f, a, b, e, d, c, dp
  // Binary_to_BCD_converter #(.binvalue(6)) binary_to_bcd_converter_3: pin names not known; wires that end beside it: OUTVAL_Second
endmodule

module DigitalClock_New (
  input  [1:0] in_1,
  input  SET,
  input  [5:0] SETVAL,
  input  in_4,
  output [5:0] OUTVAL_HOUR,
  output ACC_HOUR,
  output [5:0] OUTVAL_MINUTE,
  output [5:0] OUTVAL_Second
);

  wire and_1_out, and_2_out, and_3_out, and_4_out, clock_1_out, counter60_1_f1, counter60_2_f1,
       decoder_1_out1, decoder_1_out2, decoder_1_out3, or_1_out, or_2_out, or_3_out;

  Decoder #(.select(2)) decoder_1 (
    .out1(decoder_1_out1), .out2(decoder_1_out2), .out3(decoder_1_out3), .sel(in_1), .en(1'b1));  // open: out0
  Clock clock_1 (.out(clock_1_out));
  and and_1 (and_1_out, in_4, clock_1_out);
  and and_2 (and_2_out, decoder_1_out3, SET);
  and and_3 (and_3_out, decoder_1_out1, SET);
  and and_4 (and_4_out, decoder_1_out2, SET);
  Counter #(.max('h3f), .width(6)) counter_1 (
    .clr(ACC_HOUR), .load(SET), .up(in_4), .count(in_4), .clk(or_1_out), .D(SETVAL), .Q(OUTVAL_HOUR));  // open: carry
  or or_1 (or_1_out, and_3_out, counter60_1_f1);
  or or_2 (or_2_out, and_4_out, counter60_2_f1);
  or or_3 (or_3_out, and_2_out, and_1_out);
  Counter #(.max('h3f), .width(6)) counter_2 (
    .clr(counter60_1_f1), .load(SET), .up(in_4), .count(in_4), .clk(or_2_out), .D(SETVAL), .Q(OUTVAL_MINUTE));  // open: carry
  Counter #(.max('h3f), .width(6)) counter_3 (
    .clr(counter60_2_f1), .load(SET), .up(in_4), .count(in_4), .clk(or_3_out), .D(SETVAL), .Q(OUTVAL_Second));  // open: carry
  Counter24New counter24new_1 (.Counter24_New(OUTVAL_HOUR), .F1(ACC_HOUR));
  Counter60 counter60_1 (.Counter60(OUTVAL_MINUTE), .F1(counter60_1_f1));
  Counter60 counter60_2 (.Counter60(OUTVAL_Second), .F1(counter60_2_f1));
  LED led_1 (.in(decoder_1_out1));
  // BCD_to_7_Segment_decoder bcd_to_7_segment_decoder_1: pin names not known
  // BCD_to_7_Segment_decoder bcd_to_7_segment_decoder_2: pin names not known
  _7_Segment_Display u_7_segment_display_1 ();  // open: g, f, a, b, e, d, c, dp
  _7_Segment_Display u_7_segment_display_2 ();  // open: g, f, a, b, e, d, c, dp
  // Binary_to_BCD_converter #(.binvalue(6)) binary_to_bcd_converter_1: pin names not known; wires that end beside it: OUTVAL_HOUR
  // BCD_to_7_Segment_decoder bcd_to_7_segment_decoder_3: pin names not known
  _7_Segment_Display u_7_segment_display_3 ();  // open: g, f, a, b, e, d, c, dp
  // Binary_to_BCD_converter #(.binvalue(6)) binary_to_bcd_converter_2: pin names not known; wires that end beside it: OUTVAL_MINUTE
  LED led_2 (.in(decoder_1_out2));
  // BCD_to_7_Segment_decoder bcd_to_7_segment_decoder_4: pin names not known
  _7_Segment_Display u_7_segment_display_4 ();  // open: g, f, a, b, e, d, c, dp
  // BCD_to_7_Segment_decoder bcd_to_7_segment_decoder_5: pin names not known
  _7_Segment_Display u_7_segment_display_5 ();  // open: g, f, a, b, e, d, c, dp
  // Binary_to_BCD_converter #(.binvalue(6)) binary_to_bcd_converter_3: pin names not known; wires that end beside it: OUTVAL_Second
  LED led_3 (.in(decoder_1_out3));
  // BCD_to_7_Segment_decoder bcd_to_7_segment_decoder_6: pin names not known
  _7_Segment_Display u_7_segment_display_6 ();  // open: g, f, a, b, e, d, c, dp
endmodule

module Draft (
  input  SET_HOUR,
  input  in_2,
  input  ENABLE_HOUR,
  input  [4:0] SETVAL_HOUR,
  input  SET_MINUTE,
  input  in_6,
  input  ENABLE_MINUTE,
  input  [5:0] SETVAL_MINUTE,
  input  SET_Second,
  input  in_10,
  input  ENABLE_Second,
  input  [5:0] SETVAL_Second,
  output [4:0] OUTVAL_HOUR,
  output ACC_HOUR,
  output [5:0] OUTVAL_MINUTE,
  output [5:0] OUTVAL_Second
);

  wire and_1_out, and_2_out, CLOCK_Second_out, counter60_1_f1, counter60_2_f1, set_six_to_one_1_f1,
       set_six_to_one_2_f1;

  Clock CLOCK_Second (.out(CLOCK_Second_out));
  Counter #(.max('h1f), .width(5)) counter_1 (
    .clr(ACC_HOUR), .load(SET_HOUR), .up(in_2), .count(ENABLE_HOUR), .clk(counter60_1_f1), .D(SETVAL_HOUR),
    .Q(OUTVAL_HOUR));  // open: carry
  Counter #(.max('h3f), .width(6)) counter_2 (
    .clr(counter60_1_f1), .load(SET_MINUTE), .up(in_6), .count(ENABLE_MINUTE), .clk(counter60_2_f1),
    .D(SETVAL_MINUTE), .Q(OUTVAL_MINUTE));  // open: carry
  Counter #(.max('h3f), .width(6)) counter_3 (
    .clr(counter60_2_f1), .load(SET_Second), .up(in_10), .count(ENABLE_Second), .clk(CLOCK_Second_out),
    .D(SETVAL_Second), .Q(OUTVAL_Second));  // open: carry
  Counter24 counter24_1 (.Counter24(OUTVAL_HOUR), .F2(ACC_HOUR));
  Counter60 counter60_1 (.Counter60(OUTVAL_MINUTE), .F1(counter60_1_f1));
  Counter60 counter60_2 (.Counter60(OUTVAL_Second), .F1(counter60_2_f1));
  // BCD_to_7_Segment_decoder bcd_to_7_segment_decoder_1: pin names not known
  _7_Segment_Display u_7_segment_display_1 ();  // open: g, f, a, b, e, d, c, dp
  // Binary_to_BCD_converter #(.binvalue(5)) binary_to_bcd_converter_1: pin names not known; wires that end beside it: OUTVAL_HOUR
  SET_SIX_TO_ONE set_six_to_one_1 (.setval(OUTVAL_MINUTE), .F1(set_six_to_one_1_f1));
  SET_SIX_TO_ONE set_six_to_one_2 (.setval(OUTVAL_Second), .F1(set_six_to_one_2_f1));
  // AND_Gate and_1 has open pins: out=and_1_out
  LED led_1 (.in(and_1_out));
  // BCD_to_7_Segment_decoder bcd_to_7_segment_decoder_2: pin names not known
  _7_Segment_Display u_7_segment_display_2 ();  // open: g, f, a, b, e, d, c, dp
  and and_2 (and_2_out, set_six_to_one_1_f1, set_six_to_one_2_f1);
  LED led_2 (.in(and_2_out));
  // BCD_to_7_Segment_decoder bcd_to_7_segment_decoder_3: pin names not known
  _7_Segment_Display u_7_segment_display_3 ();  // open: g, f, a, b, e, d, c, dp
  // Binary_to_BCD_converter #(.binvalue(6)) binary_to_bcd_converter_2: pin names not known; wires that end beside it: OUTVAL_MINUTE
  // BCD_to_7_Segment_decoder bcd_to_7_segment_decoder_4: pin names not known
  _7_Segment_Display u_7_segment_display_4 ();  // open: g, f, a, b, e, d, c, dp
  // BCD_to_7_Segment_decoder bcd_to_7_segment_decoder_5: pin names not known
  // BCD_to_7_Segment_decoder bcd_to_7_segment_decoder_6: pin names not known
  _7_Segment_Display u_7_segment_display_5 ();  // open: g, f, a, b, e, d, c, dp
  _7_Segment_Display u_7_segment_display_6 ();  // open: g, f, a, b, e, d, c, dp
  // Binary_to_BCD_converter #(.binvalue(6)) binary_to_bcd_converter_3: pin names not known; wires that end beside it: OUTVAL_Second
endmodule

module Setfivetoone (
  input  [4:0] setval,
  output F1
);

  wire not_1_out, not_2_out, not_3_out, not_4_out, not_5_out;

  not not_1 (not_1_out, setval[4]);
  not not_2 (not_2_out, setval[3]);
  not not_3 (not_3_out, setval[2]);
  not not_4 (not_4_out, setval[1]);
  not not_5 (not_5_out, setval[0]);
  and and_1 (F1, not_1_out, not_2_out, not_3_out, not_4_out, not_5_out);
endmodule

module SET_SIX_TO_ONE (
  input  [5:0] setval,
  output F1
);

  wire not_1_out, not_2_out, not_3_out, not_4_out, not_5_out;

  not not_1 (not_1_out, setval[4]);
  not not_2 (not_2_out, setval[3]);
  not not_3 (not_3_out, setval[2]);
  not not_4 (not_4_out, setval[1]);
  not not_5 (not_5_out, setval[0]);
  and and_1 (F1, not_1_out, not_2_out, not_3_out, not_4_out, not_5_out);
endmodule

module Alarm_Clock (
  input  SET_HOUR,
  input  in_2,
  input  ENABLE_HOUR,
  input  [4:0] SETVAL_HOUR,
  input  SET_MINUTE,
  input  in_6,
  input  ENABLE_MINUTE,
  input  [5:0] SETVAL_MINUTE,
  input  SET_Second,
  input  in_10,
  input  ENABLE_Second,
  input  [5:0] SETVAL_Second,
  input  in_13,
  input  ALARM_HOUR_1,
  input  ALARM_HOUR_SET_ENABLE,
  input  [4:0] in_16,
  input  in_17,
  input  ALARM_MINUTE_1,
  input  ALARM_MINUTE_SET_ENABLE,
  input  [5:0] in_20,
  output [4:0] OUTVAL_HOUR,
  output ACC_HOUR,
  output [5:0] OUTVAL_MINUTE,
  output [5:0] OUTVAL_Second,
  output [4:0] out_25,
  output out_26,
  output [5:0] out_27,
  output ACC_MINUTE
);

  wire ALARM_HOUR_SET_BUTTUN_out, ALARM_MINUTE_SET_BUTTUN_out, and_1_out, CLOCK_Second_out, comparator_1_eq,
       comparator_2_eq, counter60_1_f1, counter60_2_f1;

  Clock CLOCK_Second (.out(CLOCK_Second_out));
  Button ALARM_HOUR_SET_BUTTUN (.out(ALARM_HOUR_SET_BUTTUN_out));
  Button ALARM_MINUTE_SET_BUTTUN (.out(ALARM_MINUTE_SET_BUTTUN_out));
  Counter #(.max('h1f), .width(5)) counter_1 (
    .clr(ACC_HOUR), .load(SET_HOUR), .up(in_2), .count(ENABLE_HOUR), .clk(counter60_1_f1), .D(SETVAL_HOUR),
    .Q(OUTVAL_HOUR));  // open: carry
  Counter #(.max('h3f), .width(6)) counter_2 (
    .clr(counter60_1_f1), .load(SET_MINUTE), .up(in_6), .count(ENABLE_MINUTE), .clk(counter60_2_f1),
    .D(SETVAL_MINUTE), .Q(OUTVAL_MINUTE));  // open: carry
  Counter #(.max('h3f), .width(6)) counter_3 (
    .clr(counter60_2_f1), .load(SET_Second), .up(in_10), .count(ENABLE_Second), .clk(CLOCK_Second_out),
    .D(SETVAL_Second), .Q(OUTVAL_Second));  // open: carry
  Counter #(.max('h1f), .width(5)) counter_4 (
    .clr(out_26), .load(in_13), .up(ALARM_HOUR_1), .count(ALARM_HOUR_SET_ENABLE),
    .clk(ALARM_HOUR_SET_BUTTUN_out), .D(in_16), .Q(out_25));  // open: carry
  Counter #(.max('h3f), .width(6)) counter_5 (
    .clr(ACC_MINUTE), .load(in_17), .up(ALARM_MINUTE_1), .count(ALARM_MINUTE_SET_ENABLE),
    .clk(ALARM_MINUTE_SET_BUTTUN_out), .D(in_20), .Q(out_27));  // open: carry
  Counter24 counter24_1 (.Counter24(OUTVAL_HOUR), .F2(ACC_HOUR));
  Counter60 counter60_1 (.Counter60(OUTVAL_MINUTE), .F1(counter60_1_f1));
  Counter60 counter60_2 (.Counter60(OUTVAL_Second), .F1(counter60_2_f1));
  Counter24 counter24_2 (.Counter24(out_25), .F2(out_26));
  Counter60 counter60_3 (.Counter60(out_27), .F1(ACC_MINUTE));
  // BCD_to_7_Segment_decoder bcd_to_7_segment_decoder_1: pin names not known
  _7_Segment_Display u_7_segment_display_1 ();  // open: g, f, a, b, e, d, c, dp
  // Binary_to_BCD_converter #(.binvalue(5)) binary_to_bcd_converter_1: pin names not known; wires that end beside it: out_25
  // BCD_to_7_Segment_decoder bcd_to_7_segment_decoder_2: pin names not known
  _7_Segment_Display u_7_segment_display_2 ();  // open: g, f, a, b, e, d, c, dp
  Comparator #(.width(5)) comparator_1 (.a(OUTVAL_HOUR), .b(out_25), .eq(comparator_1_eq));  // open: gt, lt
  // BCD_to_7_Segment_decoder bcd_to_7_segment_decoder_3: pin names not known
  _7_Segment_Display u_7_segment_display_3 ();  // open: g, f, a, b, e, d, c, dp
  // Binary_to_BCD_converter #(.binvalue(5)) binary_to_bcd_converter_2: pin names not known; wires that end beside it: OUTVAL_HOUR
  // BCD_to_7_Segment_decoder bcd_to_7_segment_decoder_4: pin names not known
  // BCD_to_7_Segment_decoder bcd_to_7_segment_decoder_5: pin names not known
  _7_Segment_Display u_7_segment_display_4 ();  // open: g, f, a, b, e, d, c, dp
  _7_Segment_Display u_7_segment_display_5 ();  // open: g, f, a, b, e, d, c, dp
  // Binary_to_BCD_converter #(.binvalue(6)) binary_to_bcd_converter_3: pin names not known; wires that end beside it: out_27
  // BCD_to_7_Segment_decoder bcd_to_7_segment_decoder_6: pin names not known
  _7_Segment_Display u_7_segment_display_6 ();  // open: g, f, a, b, e, d, c, dp
  // BCD_to_7_Segment_decoder bcd_to_7_segment_decoder_7: pin names not known
  _7_Segment_Display u_7_segment_display_7 ();  // open: g, f, a, b, e, d, c, dp
  // Binary_to_BCD_converter #(.binvalue(6)) binary_to_bcd_converter_4: pin names not known; wires that end beside it: OUTVAL_MINUTE
  Comparator #(.width(6)) comparator_2 (.a(OUTVAL_MINUTE), .b(out_27), .eq(comparator_2_eq));  // open: gt, lt
  // BCD_to_7_Segment_decoder bcd_to_7_segment_decoder_8: pin names not known
  _7_Segment_Display u_7_segment_display_8 ();  // open: g, f, a, b, e, d, c, dp
  and and_1 (and_1_out, comparator_1_eq, comparator_2_eq);
  LED led_1 (.in(and_1_out));
  // BCD_to_7_Segment_decoder bcd_to_7_segment_decoder_9: pin names not known
  // BCD_to_7_Segment_decoder bcd_to_7_segment_decoder_10: pin names not known
  _7_Segment_Display u_7_segment_display_9 ();  // open: g, f, a, b, e, d, c, dp
  _7_Segment_Display u_7_segment_display_10 ();  // open: g, f, a, b, e, d, c, dp
  // Binary_to_BCD_converter #(.binvalue(6)) binary_to_bcd_converter_5: pin names not known; wires that end beside it: OUTVAL_Second
endmodule

module DigitalClock_SecondChronograph (
  input  SET_HOUR,
  input  in_2,
  input  ENABLE_HOUR,
  input  [4:0] SETVAL_HOUR,
  input  SET_MINUTE,
  input  in_6,
  input  ENABLE_MINUTE,
  input  [5:0] SETVAL_MINUTE,
  input  SET_Second,
  input  in_10,
  input  ENABLE_Second,
  input  [5:0] SETVAL_Second,
  input  in_13,
  input  in_14,
  input  [5:0] in_15,
  input  [5:0] in_16,
  input  [5:0] in_17,
  output [4:0] OUTVAL_HOUR,
  output ACC_HOUR,
  output [5:0] OUTVAL_MINUTE,
  output [5:0] OUTVAL_Second,
  output [5:0] out_22,
  output ACC_Second
);

  wire and_1_out, clock_1_out, clock_2_out, CLOCK_Second_out, counter60_1_f1, counter60_2_f1, RESET_out,
       START_STOP_out;

  Button START_STOP (.out(START_STOP_out));
  Button RESET (.out(RESET_out));
  Clock CLOCK_Second (.out(CLOCK_Second_out));
  D_Flip_Flop d_ff_1 (
    .D(START_STOP_out), .clk(clock_1_out), .Q(START_STOP_out), .reset(RESET_out));  // open: Qn, preset
  Clock clock_1 (.out(clock_1_out));
  // BCD_to_7_Segment_decoder bcd_to_7_segment_decoder_1: pin names not known; wires that end beside it: in_15, in_17
  _7_Segment_Display u_7_segment_display_1 ();  // open: g, f, a, b, e, d, c, dp
  // Binary_to_BCD_converter #(.binvalue(6)) binary_to_bcd_converter_1: pin names not known
  // BCD_to_7_Segment_decoder bcd_to_7_segment_decoder_2: pin names not known
  _7_Segment_Display u_7_segment_display_2 ();  // open: g, f, a, b, e, d, c, dp
  Counter #(.max('h1f), .width(5)) counter_1 (
    .clr(ACC_HOUR), .load(SET_HOUR), .up(in_2), .count(ENABLE_HOUR), .clk(counter60_1_f1), .D(SETVAL_HOUR),
    .Q(OUTVAL_HOUR));  // open: carry
  Counter #(.max('h3f), .width(6)) counter_2 (
    .clr(counter60_1_f1), .load(SET_MINUTE), .up(in_6), .count(ENABLE_MINUTE), .clk(counter60_2_f1),
    .D(SETVAL_MINUTE), .Q(OUTVAL_MINUTE));  // open: carry
  Counter #(.max('h3f), .width(6)) counter_3 (
    .clr(counter60_2_f1), .load(SET_Second), .up(in_10), .count(ENABLE_Second), .clk(CLOCK_Second_out),
    .D(SETVAL_Second), .Q(OUTVAL_Second));  // open: carry
  and and_1 (and_1_out, START_STOP_out, clock_1_out);
  Clock clock_2 (.out(clock_2_out));
  // BCD_to_7_Segment_decoder bcd_to_7_segment_decoder_3: pin names not known
  _7_Segment_Display u_7_segment_display_3 ();  // open: g, f, a, b, e, d, c, dp
  // Binary_to_BCD_converter #(.binvalue(6)) binary_to_bcd_converter_2: pin names not known
  // BCD_to_7_Segment_decoder bcd_to_7_segment_decoder_4: pin names not known
  _7_Segment_Display u_7_segment_display_4 ();  // open: g, f, a, b, e, d, c, dp
  Counter #(.max('h3f), .width(6)) counter_4 (
    .clr(ACC_Second), .load(in_13), .up(in_14), .count(and_1_out), .clk(clock_2_out), .D(in_16), .Q(out_22));  // open: carry
  Counter24 counter24_1 (.Counter24(OUTVAL_HOUR), .F2(ACC_HOUR));
  Counter60 counter60_1 (.Counter60(OUTVAL_MINUTE), .F1(counter60_1_f1));
  Counter60 counter60_2 (.Counter60(OUTVAL_Second), .F1(counter60_2_f1));
  // BCD_to_7_Segment_decoder bcd_to_7_segment_decoder_5: pin names not known
  // BCD_to_7_Segment_decoder bcd_to_7_segment_decoder_6: pin names not known
  _7_Segment_Display u_7_segment_display_5 ();  // open: g, f, a, b, e, d, c, dp
  _7_Segment_Display u_7_segment_display_6 ();  // open: g, f, a, b, e, d, c, dp
  // Binary_to_BCD_converter #(.binvalue(6)) binary_to_bcd_converter_3: pin names not known; wires that end beside it: out_22
  Counter60 counter60_3 (.Counter60(out_22), .F1(ACC_Second));
  // BCD_to_7_Segment_decoder bcd_to_7_segment_decoder_7: pin names not known
  _7_Segment_Display u_7_segment_display_7 ();  // open: g, f, a, b, e, d, c, dp
  // Binary_to_BCD_converter #(.binvalue(5)) binary_to_bcd_converter_4: pin names not known; wires that end beside it: OUTVAL_HOUR
  // BCD_to_7_Segment_decoder bcd_to_7_segment_decoder_8: pin names not known
  _7_Segment_Display u_7_segment_display_8 ();  // open: g, f, a, b, e, d, c, dp
  // BCD_to_7_Segment_decoder bcd_to_7_segment_decoder_9: pin names not known
  _7_Segment_Display u_7_segment_display_9 ();  // open: g, f, a, b, e, d, c, dp
  // Binary_to_BCD_converter #(.binvalue(6)) binary_to_bcd_converter_5: pin names not known; wires that end beside it: OUTVAL_MINUTE
  // BCD_to_7_Segment_decoder bcd_to_7_segment_decoder_10: pin names not known
  _7_Segment_Display u_7_segment_display_10 ();  // open: g, f, a, b, e, d, c, dp
  // BCD_to_7_Segment_decoder bcd_to_7_segment_decoder_11: pin names not known
  // BCD_to_7_Segment_decoder bcd_to_7_segment_decoder_12: pin names not known
  _7_Segment_Display u_7_segment_display_11 ();  // open: g, f, a, b, e, d, c, dp
  _7_Segment_Display u_7_segment_display_12 ();  // open: g, f, a, b, e, d, c, dp
  // Binary_to_BCD_converter #(.binvalue(6)) binary_to_bcd_converter_6: pin names not known; wires that end beside it: OUTVAL_Second
endmodule

module CLOCK_DIV (
  output CLK1000HZ,
  output CLK8HZ,
  output CLK4HZ,
  output CLK2HZ,
  output CLK1HZ
);

  wire clock_1_out, clock_2_out, clock_3_out, clock_4_out, clock_5_out;
  wire [1:0] counter_3_q, undriven;
  wire [2:0] counter_4_q, undriven_3;
  wire [3:0] counter_1_q, counter_5_q, undriven_2, undriven_5;
  wire [6:0] counter_2_q, undriven_4;

  Clock clock_1 (.out(clock_1_out));
  // NoConnect on undriven
  Clock clock_2 (.out(clock_2_out));
  Clock clock_3 (.out(clock_3_out));
  // NoConnect on undriven_3
  Clock clock_4 (.out(clock_4_out));
  // NoConnect on undriven_2
  Counter #(.max('hf), .width(4)) counter_1 (
    .clr(CLK1000HZ), .load(1'b0), .up(1'b1), .count(1'b1), .clk(clock_5_out), .D(undriven_5), .Q(counter_1_q));  // open: carry
  Clock clock_5 (.out(clock_5_out));
  // NoConnect on undriven_5
  Counter #(.max('h7f), .width(7)) counter_2 (
    .clr(CLK8HZ), .load(1'b0), .up(1'b1), .count(1'b1), .clk(CLK1000HZ), .D(undriven_4), .Q(counter_2_q));  // open: carry
  // NoConnect on undriven_4
  Counter #(.max('h3), .width(2)) counter_3 (
    .clr(CLK4HZ), .load(1'b0), .up(1'b1), .count(1'b1), .clk(CLK8HZ), .D(undriven), .Q(counter_3_q));  // open: carry
  Counter #(.max('h7), .width(3)) counter_4 (
    .clr(CLK2HZ), .load(1'b0), .up(1'b1), .count(1'b1), .clk(CLK8HZ), .D(undriven_3), .Q(counter_4_q));  // open: carry
  Counter #(.max('hf), .width(4)) counter_5 (
    .clr(CLK1HZ), .load(1'b0), .up(1'b1), .count(1'b1), .clk(CLK8HZ), .D(undriven_2), .Q(counter_5_q));  // open: carry
  Counter125 counter125_1 (.A1(counter_2_q), .F1(CLK8HZ));
  Counter2 counter2_1 (.A1(counter_3_q), .F1(CLK4HZ));
  Counter4 counter4_1 (.A1(counter_4_q), .F1(CLK2HZ));
  Counter8 counter8_1 (.A(counter_5_q), .F(CLK1HZ));
  Counter8 counter8_2 (.A(counter_1_q), .F(CLK1000HZ));
endmodule

module Counter60 (
  input  [5:0] Counter60,
  output F1
);

  wire not_1_out, not_2_out;

  not not_1 (not_1_out, Counter60[1]);
  not not_2 (not_2_out, Counter60[0]);
  and and_1 (F1, Counter60[5], Counter60[4], Counter60[3], Counter60[2], not_1_out, not_2_out);
endmodule

module Counter24 (
  input  [4:0] Counter24,
  output F2
);

  wire not_1_out, not_2_out, not_3_out;

  not not_1 (not_1_out, Counter24[2]);
  not not_2 (not_2_out, Counter24[1]);
  not not_3 (not_3_out, Counter24[0]);
  and and_1 (F2, Counter24[4], Counter24[3], not_1_out, not_2_out, not_3_out);
endmodule

module SecondChronograph (
  input  Reset,
  input  Start,
  output [5:0] OUTVAL_Second
);

  wire CLOCK_Second_out, counter60_1_f1;
  wire [5:0] counter_2_q;

  Clock CLOCK_Second (.out(CLOCK_Second_out));
  Counter #(.max('h3f), .width(6)) counter_1 (
    .clr(counter60_1_f1), .load(Reset), .up(Start), .count(Start), .clk(CLOCK_Second_out), .Q(OUTVAL_Second));  // open: D, carry
  Counter #(.max('h3f), .width(6)) counter_2 (
    .clr(Reset), .load(Reset), .clk(counter60_1_f1), .Q(counter_2_q));  // open: up, count, D, carry
  Counter60 counter60_1 (.Counter60(OUTVAL_Second), .F1(counter60_1_f1));
  // BCD_to_7_Segment_decoder bcd_to_7_segment_decoder_1: pin names not known
  _7_Segment_Display u_7_segment_display_1 ();  // open: g, f, a, b, e, d, c, dp
  // Binary_to_BCD_converter #(.binvalue(6)) binary_to_bcd_converter_1: pin names not known; wires that end beside it: counter_2_q
  // BCD_to_7_Segment_decoder bcd_to_7_segment_decoder_2: pin names not known
  _7_Segment_Display u_7_segment_display_2 ();  // open: g, f, a, b, e, d, c, dp
  // BCD_to_7_Segment_decoder bcd_to_7_segment_decoder_3: pin names not known
  _7_Segment_Display u_7_segment_display_3 ();  // open: g, f, a, b, e, d, c, dp
  // Binary_to_BCD_converter #(.binvalue(6)) binary_to_bcd_converter_2: pin names not known; wires that end beside it: OUTVAL_Second
  // BCD_to_7_Segment_decoder bcd_to_7_segment_decoder_4: pin names not known
  _7_Segment_Display u_7_segment_display_4 ();  // open: g, f, a, b, e, d, c, dp
endmodule

module Counter24New (
  input  [5:0] Counter24_New,
  output F1
);

  wire not_1_out, not_2_out;

  not not_1 (not_1_out, Counter24_New[5]);
  not not_2 (not_2_out, Counter24_New[3]);
  and and_1 (F1, not_1_out, Counter24_New[4], not_2_out, Counter24_New[2], Counter24_New[1], Counter24_New[0]);
endmodule

module Alarm_SET_Draft (
  input  in_1,
  input  in_2,
  input  STOP_ALARM,
  input  ENABLREALARM0,
  input  SETALARM0,
  input  [1:0] HMSSELECT0,
  input  [5:0] ALARMVAL0,
  input  STOPALARM0,
  input  [5:0] TIMEHOUR0,
  input  [5:0] TIMEMIN0,
  input  [5:0] TIMESEC0,
  input  CLK0,
  output [5:0] ALARMHOUR0,
  output [5:0] ALARMMIN0,
  output [5:0] ALARMSEC0,
  output SETHOUR0,
  output SETMIN0,
  output SETSEC0,
  output ALARMSIG0
);

  wire and_1_out, CLK_out, comparator_1_eq, comparator_2_eq, comparator_3_eq, multiplexer_1_out,
       multiplexer_2_out;

  Decoder #(.select(2)) decoder_1 (
    .out1(SETSEC0), .out2(SETHOUR0), .out3(SETMIN0), .sel(HMSSELECT0), .en(SETALARM0));  // open: out0
  Comparator #(.width(6)) comparator_1 (.a(ALARMHOUR0), .b(TIMEHOUR0), .eq(comparator_1_eq));  // open: gt, lt
  Comparator #(.width(6)) comparator_2 (.a(ALARMMIN0), .b(TIMEMIN0), .eq(comparator_2_eq));  // open: gt, lt
  Comparator #(.width(6)) comparator_3 (.a(ALARMSEC0), .b(TIMESEC0), .eq(comparator_3_eq));  // open: gt, lt
  and and_1 (and_1_out, comparator_1_eq, comparator_2_eq, comparator_3_eq, ENABLREALARM0);
  Multiplexer multiplexer_1 (.in0(in_1), .in1(in_2), .out(multiplexer_1_out), .sel(STOPALARM0));
  Clock CLK (.out(CLK_out));
  Multiplexer multiplexer_2 (.in0(and_1_out), .in1(CLK_out), .out(multiplexer_2_out), .sel(STOP_ALARM));
  D_Flip_Flop d_ff_1 (.D(multiplexer_1_out), .clk(multiplexer_2_out), .Q(ALARMSIG0));  // open: Qn, preset, reset
  Register #(.width(6)) HOUR (.D(ALARMVAL0), .en(SETHOUR0), .clk(CLK0), .Q(ALARMHOUR0));  // open: clr
  Register #(.width(6)) MIN (.D(ALARMVAL0), .en(SETMIN0), .clk(CLK0), .Q(ALARMMIN0));  // open: clr
  Register #(.width(6)) SEC (.D(ALARMVAL0), .en(SETSEC0), .clk(CLK0), .Q(ALARMSEC0));  // open: clr

  // Other names for the same wires on the sheet: ALARMHOUR[5:0] = ALARMHOUR0; ALARMMIN[5:0] = ALARMMIN0;
  //   ALARMSEC[5:0] = ALARMSEC0; ALARMSIG = ALARMSIG0; ALARMVAL[5:0] = ALARMVAL0; CLK = CLK0;
  //   ENABLEALARM = ENABLREALARM0; HMSSELECT[1:0] = HMSSELECT0; SETALARM = SETALARM0; SETHOUR = SETHOUR0;
  //   SETMIN = SETMIN0; SETSEC = SETSEC0; STOPALARM = STOPALARM0; TIMEHOUR[5:0] = TIMEHOUR0; TIMEMIN[5:0] = TIMEMIN0;
  //   TIMESEC[5:0] = TIMESEC0
endmodule

module ONE_TO_SIX (
  input  A1,
  output [5:0] F1
);


  assign F1 = {6{A1}};
endmodule

module MOD38 (
  input  [5:0] A,
  output F
);

  wire not_1_out, not_2_out, not_3_out;

  not not_1 (not_1_out, A[4]);
  not not_2 (not_2_out, A[3]);
  not not_3 (not_3_out, A[0]);
  and and_1 (F, A[5], not_1_out, not_2_out, A[2], A[1], not_3_out);
endmodule

module MOD31 (
  input  [5:0] A,
  output F
);

  wire not_1_out;

  not not_1 (not_1_out, A[5]);
  and and_1 (F, not_1_out, A[4], A[3], A[2], A[1], A[0]);
endmodule

module MUSIC_NOTES (
  input  in_1,
  input  in_2,
  input  in_3,
  input  in_4,
  input  in_5,
  input  in_6,
  input  in_7,
  input  in_8,
  input  in_9,
  input  in_10,
  input  in_11,
  input  in_12,
  input  in_13,
  input  in_14
);

  wire clock_1_out, clock_2_out, clock_3_out, clock_4_out, clock_5_out, clock_6_out, clock_7_out, DO_NOTE,
       FA_NOTE, LA_NOTE, MI_NOTE, RE_NOTE, SO_NOTE, XI_NOTE;
  wire [3:0] counter_1_q, counter_2_q, counter_3_q, counter_4_q, counter_5_q, counter_6_q, counter_7_q;

  Clock clock_1 (.out(clock_1_out));
  Clock clock_2 (.out(clock_2_out));
  Clock clock_3 (.out(clock_3_out));
  Clock clock_4 (.out(clock_4_out));
  Counter #(.max('hf), .width(4)) counter_1 (
    .clr(DO_NOTE), .load(in_1), .up(in_3), .count(in_3), .clk(clock_1_out), .Q(counter_1_q));  // open: D, carry
  Counter #(.max('hf), .width(4)) counter_2 (
    .clr(RE_NOTE), .load(in_5), .up(in_7), .count(in_7), .clk(clock_2_out), .Q(counter_2_q));  // open: D, carry
  Counter #(.max('hf), .width(4)) counter_3 (
    .clr(MI_NOTE), .load(in_9), .up(in_10), .count(in_10), .clk(clock_3_out), .Q(counter_3_q));  // open: D, carry
  Counter #(.max('hf), .width(4)) counter_4 (
    .clr(FA_NOTE), .load(in_13), .up(in_14), .count(in_14), .clk(clock_4_out), .Q(counter_4_q));  // open: D, carry
  Counter8 counter8_1 (.A(counter_1_q), .F(DO_NOTE));
  Counter8 counter8_2 (.A(counter_2_q), .F(RE_NOTE));
  Counter8 counter8_3 (.A(counter_4_q), .F(FA_NOTE));
  Counter8 counter8_4 (.A(counter_3_q), .F(MI_NOTE));
  Clock clock_5 (.out(clock_5_out));
  Clock clock_6 (.out(clock_6_out));
  Clock clock_7 (.out(clock_7_out));
  Counter #(.max('hf), .width(4)) counter_5 (
    .clr(SO_NOTE), .load(in_2), .up(in_4), .count(in_4), .clk(clock_5_out), .Q(counter_5_q));  // open: D, carry
  Counter #(.max('hf), .width(4)) counter_6 (
    .clr(LA_NOTE), .load(in_6), .up(in_8), .count(in_8), .clk(clock_6_out), .Q(counter_6_q));  // open: D, carry
  Counter #(.max('hf), .width(4)) counter_7 (
    .clr(XI_NOTE), .load(in_11), .up(in_12), .count(in_12), .clk(clock_7_out), .Q(counter_7_q));  // open: D, carry
  Counter8 counter8_5 (.A(counter_6_q), .F(LA_NOTE));
  Counter8 counter8_6 (.A(counter_5_q), .F(SO_NOTE));
  Counter8 counter8_7 (.A(counter_7_q), .F(XI_NOTE));
endmodule

module Counter15 (
  input  [3:0] A,
  output F
);

  and and_1 (F, A[3], A[2], A[1], A[0]);
endmodule

module Counter8 (
  input  [3:0] A,
  output F
);

  wire not_1_out, not_2_out, not_3_out;

  not not_1 (not_1_out, A[2]);
  not not_2 (not_2_out, A[1]);
  not not_3 (not_3_out, A[0]);
  and and_1 (F, A[3], not_1_out, not_2_out, not_3_out);
endmodule

module Counter125 (
  input  [6:0] A1,
  output F1
);

  wire not_1_out;

  not not_1 (not_1_out, A1[1]);
  and and_1 (F1, A1[6], A1[5], A1[4], A1[3], A1[2], A1[0], not_1_out);
endmodule

module Counter4 (
  input  [2:0] A1,
  output F1
);

  wire not_1_out, not_2_out;

  not not_1 (not_1_out, A1[1]);
  not not_2 (not_2_out, A1[0]);
  and and_1 (F1, A1[2], not_2_out, not_1_out);
endmodule

module Counter2 (
  input  [1:0] A1,
  output F1
);

  wire not_1_out;

  not not_1 (not_1_out, A1[0]);
  and and_1 (F1, A1[1], not_1_out);
endmodule

module Test1 (
  input  in_1,
  input  [6:0] in_2,
  input  in_3,
  input  [6:0] in_4,
  input  [13:0] in_5,
  input  [13:0] in_6,
  input  [13:0] in_7,
  input  [13:0] in_8,
  input  in_9,
  input  [13:0] in_10,
  input  [2:0] in_11,
  input  in_12,
  input  [13:0] in_13,
  input  [13:0] in_14,
  output [13:0] out_15,
  output [3:0] out_16
);

  wire clock_1_out, counter8_1_f, counter_1_carry;
  wire [13:0] multiplexer_2_out;

  Multiplexer #(.select(3), .width(14)) multiplexer_1 (
    .in1(in_5), .in2(in_6), .in3(in_7), .in4(in_8), .in5(in_10), .in6(in_13), .in7(in_14), .out(out_15),
    .sel(in_11));  // open: in0
  // Buzzer buzzer_1: pin names not known; wires that end beside it: 14'h262, in_1, in_2
  Multiplexer #(.select(4), .width(14)) multiplexer_2 (
    .in1(14'h262), .in2(14'h294), .in3(14'h330), .in4(14'h349), .in5(14'h392), .in6(14'h440), .in7(14'h494),
    .out(multiplexer_2_out), .sel(out_16));  // open: in0, in8, in9, in10, in11, in12, in13, in14, in15
  Counter #(.max('hf), .width(4)) counter_1 (
    .clr(counter8_1_f), .load(in_9), .up(in_12), .count(in_12), .clk(clock_1_out), .carry(counter_1_carry),
    .Q(out_16));  // open: D
  Clock clock_1 (.out(clock_1_out));
  // Buzzer buzzer_2: pin names not known; wires that end beside it: multiplexer_2_out, in_3, in_4, counter_1_carry
  Counter8 counter8_1 (.A(out_16), .F(counter8_1_f));
endmodule

module MOD7 (
  input  [2:0] A,
  output F
);

  and and_1 (F, A[2], A[1], A[0]);
endmodule

module test2 (
  input  in_1,
  input  [6:0] in_2,
  input  SET_MINUTE,
  input  in_4,
  input  ENABLE_MINUTE,
  output [5:0] OUTVAL_MINUTE,
  output ACC_MINUTE
);

  wire CLK1HZ, CLK2HZ, CLK4HZ, CLK8HZ, CLK1000HZ, undriven;
  wire [13:0] buzzer_do_2_m1_do;

  Clock clock_1 ();  // open: out
  Counter #(.max('h3f), .width(6)) counter_1 (
    .clr(ACC_MINUTE), .load(SET_MINUTE), .up(in_4), .count(ENABLE_MINUTE), .clk(undriven), .Q(OUTVAL_MINUTE));  // open: D, carry
  CLOCK_DIV clock_div_1 (.CLK1000HZ(CLK1000HZ), .CLK8HZ(CLK8HZ), .CLK4HZ(CLK4HZ), .CLK2HZ(CLK2HZ), .CLK1HZ(CLK1HZ));
  // BCD_to_7_Segment_decoder bcd_to_7_segment_decoder_1: pin names not known
  _7_Segment_Display u_7_segment_display_1 ();  // open: g, f, a, b, e, d, c, dp
  // BCD_to_7_Segment_decoder bcd_to_7_segment_decoder_2: pin names not known
  _7_Segment_Display u_7_segment_display_2 ();  // open: g, f, a, b, e, d, c, dp
  // Binary_to_BCD_converter #(.binvalue(6)) binary_to_bcd_converter_1: pin names not known; wires that end beside it: OUTVAL_MINUTE
  Counter60 counter60_1 (.Counter60(OUTVAL_MINUTE), .F1(ACC_MINUTE));
  Buzzer_Do buzzer_do_1 ();  // open: CLK_8kHz, M1_Do, N1_Do
  Buzzer_Do buzzer_do_2 (.M1_Do(buzzer_do_2_m1_do));  // open: CLK_8kHz, N1_Do
  // Buzzer buzzer_1: pin names not known; wires that end beside it: buzzer_do_2_m1_do, in_1, in_2
endmodule

module Buzzer_Do (
  input  CLK_8kHz,
  output [13:0] M1_Do,
  output N1_Do
);

  wire counter15_1_f;
  wire [1:0] counter_2_q;
  wire [3:0] counter_1_q;

  Counter #(.max('hf), .width(4)) counter_1 (
    .clr(counter15_1_f), .load(1'b0), .up(1'b1), .count(1'b1), .clk(CLK_8kHz), .Q(counter_1_q));  // open: D, carry
  Counter #(.max('h3), .width(2)) counter_2 (
    .clr(N1_Do), .load(1'b0), .up(1'b1), .count(1'b1), .clk(counter15_1_f), .Q(counter_2_q));  // open: D, carry
  Counter15 counter15_1 (.A(counter_1_q), .F(counter15_1_f));
  Counter2 counter2_1 (.A1(counter_2_q), .F1(N1_Do));

  assign M1_Do = 14'h106;
endmodule

module Buzzer_Do_pro (
  input  CLK_8kHz,
  output [13:0] M1_Do1pro,
  output N1_dopro
);

  wire counter8_1_f;
  wire [1:0] counter_2_q;
  wire [3:0] counter_1_q;

  Counter #(.max('hf), .width(4)) counter_1 (
    .clr(counter8_1_f), .load(1'b0), .up(1'b1), .count(1'b1), .clk(CLK_8kHz), .Q(counter_1_q));  // open: D, carry
  Counter #(.max('h3), .width(2)) counter_2 (
    .clr(N1_dopro), .load(1'b0), .up(1'b1), .count(1'b1), .clk(counter8_1_f), .Q(counter_2_q));  // open: D, carry
  Counter8 counter8_1 (.A(counter_1_q), .F(counter8_1_f));
  Counter2 counter2_1 (.A1(counter_2_q), .F1(N1_dopro));

  assign M1_Do1pro = 14'h20b;
endmodule

module Buzzer_Re (
  input  CLK_8kHz,
  output [13:0] M1_Re,
  output N1_Re
);

  wire counter14_1_f;
  wire [1:0] counter_2_q;
  wire [3:0] counter_1_q;

  Counter #(.max('hf), .width(4)) counter_1 (
    .clr(counter14_1_f), .load(1'b0), .up(1'b1), .count(1'b1), .clk(CLK_8kHz), .Q(counter_1_q));  // open: D, carry
  Counter #(.max('h3), .width(2)) counter_2 (
    .clr(N1_Re), .load(1'b0), .up(1'b1), .count(1'b1), .clk(counter14_1_f), .Q(counter_2_q));  // open: D, carry
  Counter14 counter14_1 (.A(counter_1_q), .F(counter14_1_f));
  Counter2 counter2_1 (.A1(counter_2_q), .F1(N1_Re));

  assign M1_Re = 14'h126;
endmodule

module Buzzer_Re2_pro (
  input  CLK_8kHz,
  output [13:0] M1_Re2pro,
  output N1_Re2pro
);

  wire counter7_1_f;
  wire [1:0] counter_2_q;
  wire [3:0] counter_1_q;

  Counter #(.max('hf), .width(4)) counter_1 (
    .clr(counter7_1_f), .load(1'b0), .up(1'b1), .count(1'b1), .clk(CLK_8kHz), .Q(counter_1_q));  // open: D, carry
  Counter #(.max('h3), .width(2)) counter_2 (
    .clr(N1_Re2pro), .load(1'b0), .up(1'b1), .count(1'b1), .clk(counter7_1_f), .Q(counter_2_q));  // open: D, carry
  Counter7 counter7_1 (.A(counter_1_q), .F(counter7_1_f));
  Counter2 counter2_1 (.A1(counter_2_q), .F1(N1_Re2pro));

  assign M1_Re2pro = 14'h24b;
endmodule

module Buzzer_Mi3 (
  input  CLK_8kHz,
  output [13:0] M1_Mi3,
  output N1_Mi3
);

  wire counter12_1_f;
  wire [1:0] counter_2_q;
  wire [3:0] counter_1_q;

  Counter #(.max('hf), .width(4)) counter_1 (
    .clr(counter12_1_f), .load(1'b0), .up(1'b1), .count(1'b1), .clk(CLK_8kHz), .Q(counter_1_q));  // open: D, carry
  Counter #(.max('h3), .width(2)) counter_2 (
    .clr(N1_Mi3), .load(1'b0), .up(1'b1), .count(1'b1), .clk(counter12_1_f), .Q(counter_2_q));  // open: D, carry
  Counter12 counter12_1 (.A(counter_1_q), .F(counter12_1_f));
  Counter2 counter2_1 (.A1(counter_2_q), .F1(N1_Mi3));

  assign M1_Mi3 = 14'h14a;
endmodule

module Buzzer_Mi3pro (
  input  CLK_8kHz,
  output [13:0] M1_Mi3,
  output N1_Mi3
);

  wire counter8_1_f;
  wire [1:0] counter_2_q;
  wire [3:0] counter_1_q;

  Counter #(.max('hf), .width(4)) counter_1 (
    .clr(counter8_1_f), .load(1'b0), .up(1'b1), .count(1'b1), .clk(CLK_8kHz), .Q(counter_1_q));  // open: D, carry
  Counter #(.max('h3), .width(2)) counter_2 (
    .clr(N1_Mi3), .load(1'b0), .up(1'b1), .count(1'b1), .clk(counter8_1_f), .Q(counter_2_q));  // open: D, carry
  Counter8 counter8_1 (.A(counter_1_q), .F(counter8_1_f));
  Counter2 counter2_1 (.A1(counter_2_q), .F1(N1_Mi3));

  assign M1_Mi3 = 14'h293;
endmodule

module Buzzer_Fa4 (
  input  CLK_8kHz,
  output [13:0] M1_Fa4,
  output N1_Fa4
);

  wire counter11_1_f;
  wire [1:0] counter_2_q;
  wire [3:0] counter_1_q;

  Counter #(.max('hf), .width(4)) counter_1 (
    .clr(counter11_1_f), .load(1'b0), .up(1'b1), .count(1'b1), .clk(CLK_8kHz), .Q(counter_1_q));  // open: D, carry
  Counter #(.max('h3), .width(2)) counter_2 (
    .clr(N1_Fa4), .load(1'b0), .up(1'b1), .count(1'b1), .clk(counter11_1_f), .Q(counter_2_q));  // open: D, carry
  Counter11 counter11_1 (.A(counter_1_q), .F(counter11_1_f));
  Counter2 counter2_1 (.A1(counter_2_q), .F1(N1_Fa4));

  assign M1_Fa4 = 14'h15d;
endmodule

module Buzzer_Fa4_pro (
  input  CLK_8kHz,
  output [13:0] M1_Fa4pro,
  output N1_Fa4pro
);

  wire mod7_1_f;
  wire [1:0] counter_2_q;
  wire [2:0] counter_1_q;

  Counter #(.max('h7), .width(3)) counter_1 (
    .clr(mod7_1_f), .load(1'b0), .up(1'b1), .count(1'b1), .clk(CLK_8kHz), .Q(counter_1_q));  // open: D, carry
  Counter #(.max('h3), .width(2)) counter_2 (
    .clr(N1_Fa4pro), .load(1'b0), .up(1'b1), .count(1'b1), .clk(mod7_1_f), .Q(counter_2_q));  // open: D, carry
  MOD7 mod7_1 (.A(counter_1_q), .F(mod7_1_f));
  Counter2 counter2_1 (.A1(counter_2_q), .F1(N1_Fa4pro));

  assign M1_Fa4pro = 14'h2ba;
endmodule

module Buzzer_So5 (
  input  CLK_8kHz,
  output [13:0] M1_So5,
  output N1_So5
);

  wire counter10_1_f;
  wire [1:0] counter_2_q;
  wire [3:0] counter_1_q;

  Counter #(.max('hf), .width(4)) counter_1 (
    .clr(counter10_1_f), .load(1'b0), .up(1'b1), .count(1'b1), .clk(CLK_8kHz), .Q(counter_1_q));  // open: D, carry
  Counter #(.max('h3), .width(2)) counter_2 (
    .clr(N1_So5), .load(1'b0), .up(1'b1), .count(1'b1), .clk(counter10_1_f), .Q(counter_2_q));  // open: D, carry
  Counter10 counter10_1 (.A(counter_1_q), .F(counter10_1_f));
  Counter2 counter2_1 (.A1(counter_2_q), .F1(N1_So5));

  assign M1_So5 = 14'h188;
endmodule

module Buzzer_So5_pro (
  input  CLK_8kHz,
  output [13:0] M1_So5pro,
  output N1_So5pro
);

  wire counter5_1_f;
  wire [1:0] counter_2_q;
  wire [3:0] counter_1_q;

  Counter #(.max('hf), .width(4)) counter_1 (
    .clr(counter5_1_f), .load(1'b0), .up(1'b1), .count(1'b1), .clk(CLK_8kHz), .Q(counter_1_q));  // open: D, carry
  Counter #(.max('h3), .width(2)) counter_2 (
    .clr(N1_So5pro), .load(1'b0), .up(1'b1), .count(1'b1), .clk(counter5_1_f), .Q(counter_2_q));  // open: D, carry
  Counter5 counter5_1 (.A(counter_1_q), .F(counter5_1_f));
  Counter2 counter2_1 (.A1(counter_2_q), .F1(N1_So5pro));

  assign M1_So5pro = 14'h310;
endmodule

module Buzzer_La6 (
  input  CLK_8kHz,
  output [13:0] M1_La6,
  output N1_La6
);

  wire counter9_1_f;
  wire [1:0] counter_2_q;
  wire [3:0] counter_1_q;

  Counter #(.max('hf), .width(4)) counter_1 (
    .clr(counter9_1_f), .load(1'b0), .up(1'b1), .count(1'b1), .clk(CLK_8kHz), .Q(counter_1_q));  // open: D, carry
  Counter #(.max('h3), .width(2)) counter_2 (
    .clr(N1_La6), .load(1'b0), .up(1'b1), .count(1'b1), .clk(counter9_1_f), .Q(counter_2_q));  // open: D, carry
  Counter9 counter9_1 (.A(counter_1_q), .F(counter9_1_f));
  Counter2 counter2_1 (.A1(counter_2_q), .F1(N1_La6));

  assign M1_La6 = 14'h1b8;
endmodule

module Buzzer_La6_pro (
  input  CLK_8kHz,
  output [13:0] M1_La6pro,
  output N1_La6pro
);

  wire counter5_1_f;
  wire [1:0] counter_2_q;
  wire [3:0] counter_1_q;

  Counter #(.max('hf), .width(4)) counter_1 (
    .clr(counter5_1_f), .load(1'b0), .up(1'b1), .count(1'b1), .clk(CLK_8kHz), .Q(counter_1_q));  // open: D, carry
  Counter #(.max('h3), .width(2)) counter_2 (
    .clr(N1_La6pro), .load(1'b0), .up(1'b1), .count(1'b1), .clk(counter5_1_f), .Q(counter_2_q));  // open: D, carry
  Counter5 counter5_1 (.A(counter_1_q), .F(counter5_1_f));
  Counter2 counter2_1 (.A1(counter_2_q), .F1(N1_La6pro));

  assign M1_La6pro = 14'h370;
endmodule

module Buzzer_Xi7 (
  input  CLK_8kHz,
  output [13:0] M1_Xi7,
  output N1_Xi7
);

  wire counter8_1_f;
  wire [1:0] counter_2_q;
  wire [3:0] counter_1_q;

  Counter #(.max('hf), .width(4)) counter_1 (
    .clr(counter8_1_f), .load(1'b0), .up(1'b1), .count(1'b1), .clk(CLK_8kHz), .Q(counter_1_q));  // open: D, carry
  Counter #(.max('h3), .width(2)) counter_2 (
    .clr(N1_Xi7), .load(1'b0), .up(1'b1), .count(1'b1), .clk(counter8_1_f), .Q(counter_2_q));  // open: D, carry
  Counter8 counter8_1 (.A(counter_1_q), .F(counter8_1_f));
  Counter2 counter2_1 (.A1(counter_2_q), .F1(N1_Xi7));

  assign M1_Xi7 = 14'h1ee;
endmodule

module Buzzer_Xi7pro (
  input  CLK_8kHz,
  output [13:0] M1_Xi7,
  output N1_Xi7
);

  wire counter4_1_f1;
  wire [1:0] counter_2_q;
  wire [2:0] counter_1_q;

  Counter #(.max('h7), .width(3)) counter_1 (
    .clr(counter4_1_f1), .load(1'b0), .up(1'b1), .count(1'b1), .clk(CLK_8kHz), .Q(counter_1_q));  // open: D, carry
  Counter #(.max('h3), .width(2)) counter_2 (
    .clr(N1_Xi7), .load(1'b0), .up(1'b1), .count(1'b1), .clk(counter4_1_f1), .Q(counter_2_q));  // open: D, carry
  Counter4 counter4_1 (.A1(counter_1_q), .F1(counter4_1_f1));
  Counter2 counter2_1 (.A1(counter_2_q), .F1(N1_Xi7));

  assign M1_Xi7 = 14'h3dc;
endmodule

module Counter9 (
  input  [3:0] A,
  output F
);

  wire not_1_out, not_2_out;

  not not_1 (not_1_out, A[2]);
  not not_2 (not_2_out, A[1]);
  and and_1 (F, A[3], not_1_out, not_2_out, A[0]);
endmodule

module Counter52 (
  input  [5:0] A,
  output F
);

  wire not_1_out, not_2_out, not_3_out;

  not not_1 (not_1_out, A[3]);
  not not_2 (not_2_out, A[1]);
  not not_3 (not_3_out, A[0]);
  and and_1 (F, A[5], A[4], not_1_out, A[2], not_2_out, not_3_out);
endmodule

module test3 (
  input  [7:0] in_1,
  input  in_2,
  input  [6:0] in_3,
  input  in_4,
  input  [6:0] in_5,
  input  in_6,
  input  in_7,
  input  in_8,
  input  in_9,
  input  [13:0] in_10,
  input  in_11,
  input  [7:0] in_12,
  input  [6:0] in_13,
  input  in_14,
  input  [6:0] in_15,
  input  in_16,
  input  in_17
);

  wire clock_1_out, clock_2_out, clock_3_out, counter9_1_f, counter55_1_f, mod31_1_f;
  wire [3:0] counter_1_q;
  wire [5:0] counter_2_q, counter_3_q;
  wire [13:0] \do , dopro, fa, fapro, la, lapro, mi, mipro, multiplexer_1_out, multiplexer_2_out,
       multiplexer_3_out, re, repro, so, sopro, xi, xipro;

  Buzzer_Do buzzer_do_1 (.M1_Do(\do ));  // open: CLK_8kHz, N1_Do
  Buzzer_Re buzzer_re_1 (.M1_Re(re));  // open: CLK_8kHz, N1_Re
  Buzzer_Mi3 buzzer_mi3_1 (.M1_Mi3(mi));  // open: CLK_8kHz, N1_Mi3
  Buzzer_Fa4 buzzer_fa4_1 (.M1_Fa4(fa));  // open: CLK_8kHz, N1_Fa4
  Buzzer_So5 buzzer_so5_1 (.M1_So5(so));  // open: CLK_8kHz, N1_So5
  Buzzer_La6 buzzer_la6_1 (.M1_La6(la));  // open: CLK_8kHz, N1_La6
  Buzzer_Xi7 buzzer_xi7_1 (.M1_Xi7(xi));  // open: CLK_8kHz, N1_Xi7
  Buzzer_Do_pro buzzer_do_pro_1 (.M1_Do1pro(dopro));  // open: CLK_8kHz, N1_dopro
  Buzzer_Re2_pro buzzer_re2_pro_1 (.M1_Re2pro(repro));  // open: CLK_8kHz, N1_Re2pro
  Buzzer_Mi3pro buzzer_mi3pro_1 (.M1_Mi3(mipro));  // open: CLK_8kHz, N1_Mi3
  Buzzer_Fa4_pro buzzer_fa4_pro_1 (.M1_Fa4pro(fapro));  // open: CLK_8kHz, N1_Fa4pro
  Buzzer_So5_pro buzzer_so5_pro_1 (.M1_So5pro(sopro));  // open: CLK_8kHz, N1_So5pro
  Buzzer_La6_pro buzzer_la6_pro_1 (.M1_La6pro(lapro));  // open: CLK_8kHz, N1_La6pro
  Buzzer_Xi7pro buzzer_xi7pro_1 (.M1_Xi7(xipro));  // open: CLK_8kHz, N1_Xi7
  Multiplexer #(.select(4), .width(14)) multiplexer_1 (
    .out(multiplexer_1_out), .sel(counter_1_q));  // open: in0, in1, in2, in3, in4, in5, in6, in7, in8, in9, in10, in11, in12, in13, in14, in15
  Multiplexer #(.select(6), .width(14)) multiplexer_2 (
    .in0({14{1'b0}}), .in1(dopro), .in2(repro), .in3(mipro), .in4(sopro), .in5(dopro), .in6(repro),
    .in7(repro), .in8({14{1'b0}}), .in9(xi), .in10(la), .in11(so), .in12(so), .in13(so), .in14(repro),
    .in15(dopro), .in16(dopro), .in17({14{1'b0}}), .in18(dopro), .in19(repro), .in20(mipro), .in21(sopro),
    .in22(sopro), .in23(dopro), .in24(repro), .in25(repro), .in26({14{1'b0}}), .in27(repro), .in28(mipro),
    .in29(lapro), .in30(sopro), .in31(mipro), .in32(sopro), .in33(sopro), .in34({14{1'b0}}), .in35(dopro),
    .in36(repro), .in37(mipro), .in38(sopro), .in39(sopro), .in40(dopro), .in41(repro), .in42(repro),
    .in43({14{1'b0}}), .in44(xi), .in45(la), .in46(so), .in47(so), .in48(so), .in49(repro), .in50(dopro),
    .in51(dopro), .in52({14{1'b0}}), .in53({14{1'b0}}), .in54({14{1'b0}}), .out(multiplexer_2_out),
    .sel(counter_2_q));  // open: in55, in56, in57, in58, in59, in60, in61, in62, in63
  Counter #(.max('hf), .width(4)) counter_1 (
    .clr(counter9_1_f), .load(in_16), .up(in_17), .count(in_17), .clk(clock_1_out), .Q(counter_1_q));  // open: D, carry
  Clock clock_1 (.out(clock_1_out));
  Counter #(.max('h3f), .width(6)) counter_2 (
    .clr(counter55_1_f), .load(in_8), .up(in_9), .count(in_9), .clk(clock_2_out), .Q(counter_2_q));  // open: D, carry
  Clock clock_2 (.out(clock_2_out));
  // Buzzer buzzer_1: pin names not known; wires that end beside it: in_12, multiplexer_1_out, in_14, in_15
  // Buzzer #(.smooth_level(4), .smooth_width(3), .waveform("Square")) buzzer_2: pin names not known; wires that end beside it: dopro, repro, 8'h80, multiplexer_2_out, in_4, in_5
  // BCD_to_7_Segment_decoder bcd_to_7_segment_decoder_1: pin names not known
  _7_Segment_Display u_7_segment_display_1 ();  // open: g, f, a, b, e, d, c, dp
  // Binary_to_BCD_converter #(.binvalue(4)) binary_to_bcd_converter_1: pin names not known; wires that end beside it: counter_1_q
  // BCD_to_7_Segment_decoder bcd_to_7_segment_decoder_2: pin names not known
  _7_Segment_Display u_7_segment_display_2 ();  // open: g, f, a, b, e, d, c, dp
  // BCD_to_7_Segment_decoder bcd_to_7_segment_decoder_3: pin names not known
  _7_Segment_Display u_7_segment_display_3 ();  // open: g, f, a, b, e, d, c, dp
  // Binary_to_BCD_converter #(.binvalue(6)) binary_to_bcd_converter_2: pin names not known; wires that end beside it: counter_2_q
  Counter9 counter9_1 (.A(counter_1_q), .F(counter9_1_f));
  // BCD_to_7_Segment_decoder bcd_to_7_segment_decoder_4: pin names not known
  _7_Segment_Display u_7_segment_display_4 ();  // open: g, f, a, b, e, d, c, dp
  // Buzzer buzzer_3: pin names not known; wires that end beside it: in_10, in_11, in_13
  Counter55 counter55_1 (.A(counter_2_q), .F(counter55_1_f));
  Multiplexer #(.select(6), .width(14)) multiplexer_3 (
    .out(multiplexer_3_out), .sel(counter_3_q));  // open: in0, in1, in2, in3, in4, in5, in6, in7, in8, in9, in10, in11, in12, in13, in14, in15, in16, in17, in18, in19, in20, in21, in22, in23, in24, in25, in26, in27, in28, in29, in30, in31, in32, in33, in34, in35, in36, in37, in38, in39, in40, in41, in42, in43, in44, in45, in46, in47, in48, in49, in50, in51, in52, in53, in54, in55, in56, in57, in58, in59, in60, in61, in62, in63
  Counter #(.max('h3f), .width(6)) counter_3 (
    .clr(mod31_1_f), .load(in_6), .up(in_7), .count(in_7), .clk(clock_3_out), .Q(counter_3_q));  // open: D, carry
  Clock clock_3 (.out(clock_3_out));
  // Buzzer #(.smooth_width(5)) buzzer_4: pin names not known; wires that end beside it: in_1, multiplexer_3_out, in_2, in_3
  // BCD_to_7_Segment_decoder bcd_to_7_segment_decoder_5: pin names not known
  _7_Segment_Display u_7_segment_display_5 ();  // open: g, f, a, b, e, d, c, dp
  // Binary_to_BCD_converter #(.binvalue(6)) binary_to_bcd_converter_3: pin names not known; wires that end beside it: counter_3_q
  // BCD_to_7_Segment_decoder bcd_to_7_segment_decoder_6: pin names not known
  _7_Segment_Display u_7_segment_display_6 ();  // open: g, f, a, b, e, d, c, dp
  MOD31 mod31_1 (.A(counter_3_q), .F(mod31_1_f));
endmodule

module Counter34 (
  input  [5:0] A,
  output F
);

  wire not_1_out, not_2_out, not_3_out, not_4_out;

  not not_1 (not_1_out, A[4]);
  not not_2 (not_2_out, A[3]);
  not not_3 (not_3_out, A[2]);
  not not_4 (not_4_out, A[0]);
  and and_1 (F, A[5], not_1_out, not_2_out, not_3_out, A[1], not_4_out);
endmodule

module Counter55 (
  input  [5:0] A,
  output F
);

  wire not_1_out;

  not not_1 (not_1_out, A[3]);
  and and_1 (F, A[5], A[4], not_1_out, A[2], A[1], A[0]);
endmodule

module Counter14 (
  input  [3:0] A,
  output F
);

  wire not_1_out;

  not not_1 (not_1_out, A[0]);
  and and_1 (F, A[3], A[2], A[1], not_1_out);
endmodule

module Counter12 (
  input  [3:0] A,
  output F
);

  wire not_1_out, not_2_out;

  not not_1 (not_1_out, A[1]);
  not not_2 (not_2_out, A[0]);
  and and_1 (F, A[3], A[2], not_1_out, not_2_out);
endmodule

module Counter11 (
  input  [3:0] A,
  output F
);

  wire not_1_out;

  not not_1 (not_1_out, A[2]);
  and and_1 (F, A[3], not_1_out, A[1], A[0]);
endmodule

module Counter10 (
  input  [3:0] A,
  output F
);

  wire not_1_out, not_2_out;

  not not_1 (not_1_out, A[2]);
  not not_2 (not_2_out, A[0]);
  and and_1 (F, A[3], not_1_out, A[1], not_2_out);
endmodule

module Counter7 (
  input  [3:0] A,
  output F
);

  wire not_1_out;

  not not_1 (not_1_out, A[3]);
  and and_1 (F, not_1_out, A[2], A[1], A[0]);
endmodule

module Counter6 (
  input  [3:0] A,
  output F
);

  wire not_1_out, not_2_out;

  not not_1 (not_1_out, A[3]);
  not not_2 (not_2_out, A[0]);
  and and_1 (F, not_1_out, A[2], A[1], not_2_out);
endmodule

module Counter5 (
  input  [3:0] A,
  output F
);

  wire not_1_out, not_2_out;

  not not_1 (not_1_out, A[3]);
  not not_2 (not_2_out, A[1]);
  and and_1 (F, not_1_out, A[2], not_2_out, A[0]);
endmodule

module Counter4_4bit (
  input  [3:0] A,
  output F
);

  wire not_1_out, not_2_out, not_3_out;

  not not_1 (not_1_out, A[3]);
  not not_2 (not_2_out, A[1]);
  not not_3 (not_3_out, A[0]);
  and and_1 (F, not_1_out, A[2], not_2_out, not_3_out);
endmodule

module Buzzer_Do_1wHz (
  input  CLK_10kHz,
  output [13:0] M1_Do,
  output N1_Do
);

  wire counter19_1_f;
  wire [1:0] counter_2_q;
  wire [4:0] counter_1_q;

  Counter #(.max('h1f), .width(5)) counter_1 (
    .clr(counter19_1_f), .load(1'b0), .up(1'b1), .count(1'b1), .clk(CLK_10kHz), .Q(counter_1_q));  // open: D, carry
  Counter #(.max('h3), .width(2)) counter_2 (
    .clr(N1_Do), .load(1'b0), .up(1'b1), .count(1'b1), .clk(counter19_1_f), .Q(counter_2_q));  // open: D, carry
  Counter19 counter19_1 (.A(counter_1_q), .F(counter19_1_f));
  Counter2 counter2_1 (.A1(counter_2_q), .F1(N1_Do));

  assign M1_Do = 14'h106;
endmodule

module Buzzer_Dopro_1wHz (
  input  CLK_10kHz,
  output [13:0] M1_Do1pro,
  output N1_dopro
);

  wire counter10_1_f;
  wire [1:0] counter_2_q;
  wire [3:0] counter_1_q;

  Counter #(.max('hf), .width(4)) counter_1 (
    .clr(counter10_1_f), .load(1'b0), .up(1'b1), .count(1'b1), .clk(CLK_10kHz), .Q(counter_1_q));  // open: D, carry
  Counter #(.max('h3), .width(2)) counter_2 (
    .clr(N1_dopro), .load(1'b0), .up(1'b1), .count(1'b1), .clk(counter10_1_f), .Q(counter_2_q));  // open: D, carry
  Counter10 counter10_1 (.A(counter_1_q), .F(counter10_1_f));
  Counter2 counter2_1 (.A1(counter_2_q), .F1(N1_dopro));

  assign M1_Do1pro = 14'h20b;
endmodule

module Buzzer_Re_1wHz (
  input  CLK_10kHz,
  output [13:0] M1_Re,
  output N1_Re
);

  wire counter17_1_f;
  wire [1:0] counter_2_q;
  wire [4:0] counter_1_q;

  Counter #(.max('h1f), .width(5)) counter_1 (
    .clr(counter17_1_f), .load(1'b0), .up(1'b1), .count(1'b1), .clk(CLK_10kHz), .Q(counter_1_q));  // open: D, carry
  Counter #(.max('h3), .width(2)) counter_2 (
    .clr(N1_Re), .load(1'b0), .up(1'b1), .count(1'b1), .clk(counter17_1_f), .Q(counter_2_q));  // open: D, carry
  Counter17 counter17_1 (.A(counter_1_q), .F(counter17_1_f));
  Counter2 counter2_1 (.A1(counter_2_q), .F1(N1_Re));

  assign M1_Re = 14'h126;
endmodule

module Buzzer_Repro_1wHz (
  input  CLK_10kHz,
  output [13:0] M1_Re2pro,
  output N1_Re2pro
);

  wire counter8_1_f;
  wire [1:0] counter_2_q;
  wire [3:0] counter_1_q;

  Counter #(.max('hf), .width(4)) counter_1 (
    .clr(counter8_1_f), .load(1'b0), .up(1'b1), .count(1'b1), .clk(CLK_10kHz), .Q(counter_1_q));  // open: D, carry
  Counter #(.max('h3), .width(2)) counter_2 (
    .clr(N1_Re2pro), .load(1'b0), .up(1'b1), .count(1'b1), .clk(counter8_1_f), .Q(counter_2_q));  // open: D, carry
  Counter8 counter8_1 (.A(counter_1_q), .F(counter8_1_f));
  Counter2 counter2_1 (.A1(counter_2_q), .F1(N1_Re2pro));

  assign M1_Re2pro = 14'h24b;
endmodule

module Buzzer_Mi_1wHz (
  input  CLK_10kHz,
  output [13:0] M1_Mi3,
  output N1_Mi3
);

  wire counter15_1_f;
  wire [1:0] counter_2_q;
  wire [3:0] counter_1_q;

  Counter #(.max('hf), .width(4)) counter_1 (
    .clr(counter15_1_f), .load(1'b0), .up(1'b1), .count(1'b1), .clk(CLK_10kHz), .Q(counter_1_q));  // open: D, carry
  Counter #(.max('h3), .width(2)) counter_2 (
    .clr(N1_Mi3), .load(1'b0), .up(1'b1), .count(1'b1), .clk(counter15_1_f), .Q(counter_2_q));  // open: D, carry
  Counter15 counter15_1 (.A(counter_1_q), .F(counter15_1_f));
  Counter2 counter2_1 (.A1(counter_2_q), .F1(N1_Mi3));

  assign M1_Mi3 = 14'h14a;
endmodule

module Buzzer_Mipro_1wHz (
  input  CLK_10kHz,
  output [13:0] M1_Mi3,
  output N1_Mi3
);

  wire counter6_1_f;
  wire [1:0] counter_2_q;
  wire [3:0] counter_1_q;

  Counter #(.max('hf), .width(4)) counter_1 (
    .clr(counter6_1_f), .load(1'b0), .up(1'b1), .count(1'b1), .clk(CLK_10kHz), .Q(counter_1_q));  // open: D, carry
  Counter #(.max('h3), .width(2)) counter_2 (
    .clr(N1_Mi3), .load(1'b0), .up(1'b1), .count(1'b1), .clk(counter6_1_f), .Q(counter_2_q));  // open: D, carry
  Counter6 counter6_1 (.A(counter_1_q), .F(counter6_1_f));
  Counter2 counter2_1 (.A1(counter_2_q), .F1(N1_Mi3));

  assign M1_Mi3 = 14'h293;
endmodule

module Buzzer_Fa_1wHz (
  input  CLK_10kHz,
  output [13:0] M1_Fa4,
  output N1_Fa4
);

  wire counter14_1_f;
  wire [1:0] counter_2_q;
  wire [3:0] counter_1_q;

  Counter #(.max('hf), .width(4)) counter_1 (
    .clr(counter14_1_f), .load(1'b0), .up(1'b1), .count(1'b1), .clk(CLK_10kHz), .Q(counter_1_q));  // open: D, carry
  Counter #(.max('h3), .width(2)) counter_2 (
    .clr(N1_Fa4), .load(1'b0), .up(1'b1), .count(1'b1), .clk(counter14_1_f), .Q(counter_2_q));  // open: D, carry
  Counter14 counter14_1 (.A(counter_1_q), .F(counter14_1_f));
  Counter2 counter2_1 (.A1(counter_2_q), .F1(N1_Fa4));

  assign M1_Fa4 = 14'h15d;
endmodule

module Buzzer_Fapro_1wHz (
  input  CLK_10kHz,
  output [13:0] M1_Fa4pro,
  output N1_Fa4pro
);

  wire counter7_1_f;
  wire [1:0] counter_2_q;
  wire [3:0] counter_1_q;

  Counter #(.max('hf), .width(4)) counter_1 (
    .clr(counter7_1_f), .load(1'b0), .up(1'b1), .count(1'b1), .clk(CLK_10kHz), .Q(counter_1_q));  // open: D, carry
  Counter #(.max('h3), .width(2)) counter_2 (
    .clr(N1_Fa4pro), .load(1'b0), .up(1'b1), .count(1'b1), .clk(counter7_1_f), .Q(counter_2_q));  // open: D, carry
  Counter7 counter7_1 (.A(counter_1_q), .F(counter7_1_f));
  Counter2 counter2_1 (.A1(counter_2_q), .F1(N1_Fa4pro));

  assign M1_Fa4pro = 14'h2ba;
endmodule

module Buzzer_So_1wHz (
  input  CLK_10kHz,
  output [13:0] M1_So5,
  output N1_So5
);

  wire counter13_1_f;
  wire [1:0] counter_2_q;
  wire [4:0] counter_1_q;

  Counter #(.max('h1f), .width(5)) counter_1 (
    .clr(counter13_1_f), .load(1'b0), .up(1'b1), .count(1'b1), .clk(CLK_10kHz), .Q(counter_1_q));  // open: D, carry
  Counter #(.max('h3), .width(2)) counter_2 (
    .clr(N1_So5), .load(1'b0), .up(1'b1), .count(1'b1), .clk(counter13_1_f), .Q(counter_2_q));  // open: D, carry
  Counter13 counter13_1 (.A(counter_1_q), .F(counter13_1_f));
  Counter2 counter2_1 (.A1(counter_2_q), .F1(N1_So5));

  assign M1_So5 = 14'h188;
endmodule

module Buzzer_Sopro_1wHz (
  input  CLK_10kHz,
  output [13:0] M1_So5pro,
  output N1_So5pro
);

  wire counter6_1_f;
  wire [1:0] counter_2_q;
  wire [3:0] counter_1_q;

  Counter #(.max('hf), .width(4)) counter_1 (
    .clr(counter6_1_f), .load(1'b0), .up(1'b1), .count(1'b1), .clk(CLK_10kHz), .Q(counter_1_q));  // open: D, carry
  Counter #(.max('h3), .width(2)) counter_2 (
    .clr(N1_So5pro), .load(1'b0), .up(1'b1), .count(1'b1), .clk(counter6_1_f), .Q(counter_2_q));  // open: D, carry
  Counter6 counter6_1 (.A(counter_1_q), .F(counter6_1_f));
  Counter2 counter2_1 (.A1(counter_2_q), .F1(N1_So5pro));

  assign M1_So5pro = 14'h310;
endmodule

module Buzzer_La_1wHz (
  input  CLK_10kHz,
  output [13:0] M1_La6,
  output N1_La6
);

  wire counter11_1_f;
  wire [1:0] counter_2_q;
  wire [3:0] counter_1_q;

  Counter #(.max('hf), .width(4)) counter_1 (
    .clr(counter11_1_f), .load(1'b0), .up(1'b1), .count(1'b1), .clk(CLK_10kHz), .Q(counter_1_q));  // open: D, carry
  Counter #(.max('h3), .width(2)) counter_2 (
    .clr(N1_La6), .load(1'b0), .up(1'b1), .count(1'b1), .clk(counter11_1_f), .Q(counter_2_q));  // open: D, carry
  Counter11 counter11_1 (.A(counter_1_q), .F(counter11_1_f));
  Counter2 counter2_1 (.A1(counter_2_q), .F1(N1_La6));

  assign M1_La6 = 14'h1b8;
endmodule

module Buzzer_Lapro_1wHz (
  input  CLK_10kHz,
  output [13:0] M1_La6pro,
  output N1_La6pro
);

  wire counter6_1_f;
  wire [1:0] counter_2_q;
  wire [3:0] counter_1_q;

  Counter #(.max('hf), .width(4)) counter_1 (
    .clr(counter6_1_f), .load(1'b0), .up(1'b1), .count(1'b1), .clk(CLK_10kHz), .Q(counter_1_q));  // open: D, carry
  Counter #(.max('h3), .width(2)) counter_2 (
    .clr(N1_La6pro), .load(1'b0), .up(1'b1), .count(1'b1), .clk(counter6_1_f), .Q(counter_2_q));  // open: D, carry
  Counter6 counter6_1 (.A(counter_1_q), .F(counter6_1_f));
  Counter2 counter2_1 (.A1(counter_2_q), .F1(N1_La6pro));

  assign M1_La6pro = 14'h370;
endmodule

module Buzzer_Xi_1wHz (
  input  CLK_10kHz,
  output [13:0] M1_Xi7,
  output N1_Xi7
);

  wire counter10_1_f;
  wire [1:0] counter_2_q;
  wire [3:0] counter_1_q;

  Counter #(.max('hf), .width(4)) counter_1 (
    .clr(counter10_1_f), .load(1'b0), .up(1'b1), .count(1'b1), .clk(CLK_10kHz), .Q(counter_1_q));  // open: D, carry
  Counter #(.max('h3), .width(2)) counter_2 (
    .clr(N1_Xi7), .load(1'b0), .up(1'b1), .count(1'b1), .clk(counter10_1_f), .Q(counter_2_q));  // open: D, carry
  Counter10 counter10_1 (.A(counter_1_q), .F(counter10_1_f));
  Counter2 counter2_1 (.A1(counter_2_q), .F1(N1_Xi7));

  assign M1_Xi7 = 14'h1ee;
endmodule

module Buzzer_Xipro_1wHz (
  input  CLK_10kHz,
  output [13:0] M1_Xi7,
  output N1_Xi7
);

  wire counter5_1_f;
  wire [1:0] counter_2_q;
  wire [3:0] counter_1_q;

  Counter #(.max('hf), .width(4)) counter_1 (
    .clr(counter5_1_f), .load(1'b0), .up(1'b1), .count(1'b1), .clk(CLK_10kHz), .Q(counter_1_q));  // open: D, carry
  Counter #(.max('h3), .width(2)) counter_2 (
    .clr(N1_Xi7), .load(1'b0), .up(1'b1), .count(1'b1), .clk(counter5_1_f), .Q(counter_2_q));  // open: D, carry
  Counter5 counter5_1 (.A(counter_1_q), .F(counter5_1_f));
  Counter2 counter2_1 (.A1(counter_2_q), .F1(N1_Xi7));

  assign M1_Xi7 = 14'h3dc;
endmodule

module Counter19 (
  input  [4:0] A,
  output F
);

  wire not_1_out, not_2_out;

  not not_1 (not_1_out, A[3]);
  not not_2 (not_2_out, A[2]);
  and and_1 (F, A[4], not_1_out, not_2_out, A[1], A[0]);
endmodule

module Counter17 (
  input  [4:0] A,
  output F
);

  wire not_1_out, not_2_out, not_3_out;

  not not_1 (not_1_out, A[3]);
  not not_2 (not_2_out, A[2]);
  not not_3 (not_3_out, A[1]);
  and and_1 (F, A[4], not_1_out, not_2_out, not_3_out, A[0]);
endmodule

module Counter13 (
  input  [4:0] A,
  output F
);

  wire not_1_out, not_2_out;

  not not_1 (not_1_out, A[4]);
  not not_2 (not_2_out, A[1]);
  and and_1 (F, not_1_out, A[3], A[2], not_2_out, A[0]);
endmodule

module REQU_ALL_8kHz (
  input  CLK_8kHz,
  output [13:0] Buzzer_do_virtual,
  output Buzzer_do_real,
  output [13:0] Buzzer_dopro_virtual,
  output Buzzer_dopro_real,
  output [13:0] Buzzer_re_virtual,
  output Buzzer_re_real,
  output [13:0] Buzzer_repro_virtual,
  output Buzzer_repro_real,
  output [13:0] Buzzer_mi_virtual,
  output Buzzer_mi_real,
  output [13:0] Buzzer_mipro_virtual,
  output Buzzer_mipro_real,
  output [13:0] Buzzer_fa_virtual,
  output Buzzer_fa_real,
  output [13:0] Buzzer_fapro_virtual,
  output Buzzer_fapro_real,
  output [13:0] Buzzer_so_virtual,
  output Buzzer_so_real,
  output [13:0] Buzzer_sopro_virtual,
  output Buzzer_sopro_real,
  output [13:0] Buzzer_la_virtual,
  output Buzzer_la_real,
  output [13:0] Buzzer_lapro_virtual,
  output Buzzer_lapro_real,
  output [13:0] Buzzer_xi_virtual,
  output Buzzer_xi_real,
  output [13:0] Buzzer_xipro_virtual,
  output Buzzer_xipro_real
);

  Buzzer_Do buzzer_do_1 (.CLK_8kHz(CLK_8kHz), .M1_Do(Buzzer_do_virtual), .N1_Do(Buzzer_do_real));
  Buzzer_Do_pro buzzer_do_pro_1 (.CLK_8kHz(CLK_8kHz), .M1_Do1pro(Buzzer_dopro_virtual), .N1_dopro(Buzzer_dopro_real));
  Buzzer_Re buzzer_re_1 (.CLK_8kHz(CLK_8kHz), .M1_Re(Buzzer_re_virtual), .N1_Re(Buzzer_re_real));
  Buzzer_Re2_pro buzzer_re2_pro_1 (
    .CLK_8kHz(CLK_8kHz), .M1_Re2pro(Buzzer_repro_virtual), .N1_Re2pro(Buzzer_repro_real));
  Buzzer_Mi3 buzzer_mi3_1 (.CLK_8kHz(CLK_8kHz), .M1_Mi3(Buzzer_mi_virtual), .N1_Mi3(Buzzer_mi_real));
  Buzzer_Mi3pro buzzer_mi3pro_1 (.CLK_8kHz(CLK_8kHz), .M1_Mi3(Buzzer_mipro_virtual), .N1_Mi3(Buzzer_mipro_real));
  Buzzer_Fa4 buzzer_fa4_1 (.CLK_8kHz(CLK_8kHz), .M1_Fa4(Buzzer_fa_virtual), .N1_Fa4(Buzzer_fa_real));
  Buzzer_Fa4_pro buzzer_fa4_pro_1 (
    .CLK_8kHz(CLK_8kHz), .M1_Fa4pro(Buzzer_fapro_virtual), .N1_Fa4pro(Buzzer_fapro_real));
  Buzzer_So5 buzzer_so5_1 (.CLK_8kHz(CLK_8kHz), .M1_So5(Buzzer_so_virtual), .N1_So5(Buzzer_so_real));
  Buzzer_So5_pro buzzer_so5_pro_1 (
    .CLK_8kHz(CLK_8kHz), .M1_So5pro(Buzzer_sopro_virtual), .N1_So5pro(Buzzer_sopro_real));
  Buzzer_La6 buzzer_la6_1 (.CLK_8kHz(CLK_8kHz), .M1_La6(Buzzer_la_virtual), .N1_La6(Buzzer_la_real));
  Buzzer_La6_pro buzzer_la6_pro_1 (
    .CLK_8kHz(CLK_8kHz), .M1_La6pro(Buzzer_lapro_virtual), .N1_La6pro(Buzzer_lapro_real));
  Buzzer_Xi7 buzzer_xi7_1 (.CLK_8kHz(CLK_8kHz), .M1_Xi7(Buzzer_xi_virtual), .N1_Xi7(Buzzer_xi_real));
  Buzzer_Xi7pro buzzer_xi7pro_1 (.CLK_8kHz(CLK_8kHz), .M1_Xi7(Buzzer_xipro_virtual), .N1_Xi7(Buzzer_xipro_real));
endmodule

module Test4 (
);

  REQU_ALL_8kHz requ_all_8khz_1 ();  // open: CLK_8kHz, Buzzer_do_virtual, Buzzer_do_real, Buzzer_dopro_virtual, Buzzer_dopro_real, Buzzer_re_virtual, Buzzer_re_real, Buzzer_repro_virtual, Buzzer_repro_real, Buzzer_mi_virtual, Buzzer_mi_real, Buzzer_mipro_virtual, Buzzer_mipro_real, Buzzer_fa_virtual, Buzzer_fa_real, Buzzer_fapro_virtual, Buzzer_fapro_real, Buzzer_so_virtual, Buzzer_so_real, Buzzer_sopro_virtual, Buzzer_sopro_real, Buzzer_la_virtual, Buzzer_la_real, Buzzer_lapro_virtual, Buzzer_lapro_real, Buzzer_xi_virtual, Buzzer_xi_real, Buzzer_xipro_virtual, Buzzer_xipro_real
endmodule

module REQU_ALL_10Hz (
  input  CLK_10kHz,
  output [13:0] do_virtual,
  output do_real,
  output [13:0] dopro_virtual,
  output dopro_real,
  output [13:0] re_virtual,
  output re_real,
  output [13:0] repro_virtual,
  output repro_real,
  output [13:0] mi_virtual,
  output mi_real,
  output [13:0] mipro_virtual,
  output mipro_real,
  output [13:0] fa_virtual,
  output fa_real,
  output [13:0] fapro_virtual,
  output fapro_real,
  output [13:0] so_virtual,
  output so_real,
  output [13:0] sopro_virtual,
  output sopro_real,
  output [13:0] la_virtual,
  output la_real,
  output [13:0] lapro_virtual,
  output lapro_real,
  output [13:0] xi_virtual,
  output xi_real,
  output [13:0] xipro_virtual,
  output xipro_real
);

  Buzzer_Do_1wHz buzzer_do_1whz_1 (.CLK_10kHz(CLK_10kHz), .M1_Do(do_virtual), .N1_Do(do_real));
  Buzzer_Dopro_1wHz buzzer_dopro_1whz_1 (.CLK_10kHz(CLK_10kHz), .M1_Do1pro(dopro_virtual), .N1_dopro(dopro_real));
  Buzzer_Re_1wHz buzzer_re_1whz_1 (.CLK_10kHz(CLK_10kHz), .M1_Re(re_virtual), .N1_Re(re_real));
  Buzzer_Repro_1wHz buzzer_repro_1whz_1 (.CLK_10kHz(CLK_10kHz), .M1_Re2pro(repro_virtual), .N1_Re2pro(repro_real));
  Buzzer_Mi_1wHz buzzer_mi_1whz_1 (.CLK_10kHz(CLK_10kHz), .M1_Mi3(mi_virtual), .N1_Mi3(mi_real));
  Buzzer_Mipro_1wHz buzzer_mipro_1whz_1 (.CLK_10kHz(CLK_10kHz), .M1_Mi3(mipro_virtual), .N1_Mi3(mipro_real));
  Buzzer_Fa_1wHz buzzer_fa_1whz_1 (.CLK_10kHz(CLK_10kHz), .M1_Fa4(fa_virtual), .N1_Fa4(fa_real));
  Buzzer_Fapro_1wHz buzzer_fapro_1whz_1 (.CLK_10kHz(CLK_10kHz), .M1_Fa4pro(fapro_virtual), .N1_Fa4pro(fapro_real));
  Buzzer_So_1wHz buzzer_so_1whz_1 (.CLK_10kHz(CLK_10kHz), .M1_So5(so_virtual), .N1_So5(so_real));
  Buzzer_Sopro_1wHz buzzer_sopro_1whz_1 (.CLK_10kHz(CLK_10kHz), .M1_So5pro(sopro_virtual), .N1_So5pro(sopro_real));
  Buzzer_La_1wHz buzzer_la_1whz_1 (.CLK_10kHz(CLK_10kHz), .M1_La6(la_virtual), .N1_La6(la_real));
  Buzzer_Lapro_1wHz buzzer_lapro_1whz_1 (.CLK_10kHz(CLK_10kHz), .M1_La6pro(lapro_virtual), .N1_La6pro(lapro_real));
  Buzzer_Xi_1wHz buzzer_xi_1whz_1 (.CLK_10kHz(CLK_10kHz), .M1_Xi7(xi_virtual), .N1_Xi7(xi_real));
  Buzzer_Xipro_1wHz buzzer_xipro_1whz_1 (.CLK_10kHz(CLK_10kHz), .M1_Xi7(xipro_virtual), .N1_Xi7(xipro_real));
endmodule
