// Logisim project Digital_Clock_Final.circ as structural Verilog: 8 circuits, main circuit Counter6
module DigitalClock_FPGA_Final (
  input  Input_1,
  input  Input_2,
  input  [5:0] Input_bus_1,
  input  [5:0] Input_bus_2,
  input  [5:0] Input_bus_3,
  output G,
  output F,
  output A,
  output B,
  output E,
  output D,
  output C,
  output Hour_tens,
  output Hour_ones,
  output Minute_tens,
  output Minute_ones,
  output Second_tens,
  output Second_ones
);

  wire binary_to_bcd_converter_4_p2, CLK1, CLK10k, Counter6_1_output_1, Counter20_1_f, Counter24_1_output_1,
       Counter60_1_output_1, Counter60_2_output_1;
  wire [2:0] counter_6_q;
  wire [3:0] Hour_ones_t, Hour_tens_t, Minute_ones_t, Minute_tens_t, multiplexer_1_out, Second_ones_t,
       Second_tens_t;
  wire [5:0] counter_1_q, counter_2_q, counter_3_q, counter_4_q, counter_5_q;

  Clock clock_1 ();  // open: out
  Clock clock_2 (.out(CLK10k));
  Counter #(.max('h3f), .width(6)) counter_1 (
    .clr(Counter20_1_f), .load(Input_1), .up(Input_2), .count(Input_2), .clk(CLK10k), .Q(counter_1_q));  // open: D, carry
  Counter #(.max('h3f), .width(6)) counter_2 (
    .clr(Counter24_1_output_1), .load(Input_1), .up(Input_2), .count(Input_2), .clk(Counter60_1_output_1),
    .D(Input_bus_1), .Q(counter_2_q));  // open: carry
  Counter #(.max('h3f), .width(6)) counter_3 (
    .clr(Counter60_1_output_1), .load(Input_1), .up(Input_2), .count(Input_2), .clk(Counter60_2_output_1),
    .D(Input_bus_2), .Q(counter_3_q));  // open: carry
  Counter #(.max('h3f), .width(6)) counter_4 (
    .clr(Counter60_2_output_1), .load(Input_1), .up(Input_2), .count(Input_2), .clk(CLK1), .D(Input_bus_3),
    .Q(counter_4_q));  // open: carry
  Counter #(.max('h3f), .width(6)) counter_5 (
    .clr(CLK1), .load(Input_1), .up(Input_2), .count(Input_2), .clk(Counter20_1_f), .Q(counter_5_q));  // open: D, carry
  Counter20 Counter20_1 (.A(counter_1_q), .F(Counter20_1_f));
  Counter24 Counter24_1 (.Input_bus_1(counter_2_q), .Output_1(Counter24_1_output_1));
  Counter60 Counter60_1 (.Input_bus_1(counter_3_q), .Output_1(Counter60_1_output_1));
  Counter60 Counter60_2 (.Input_bus_1(counter_4_q), .Output_1(Counter60_2_output_1));
  // Binary_to_BCD_converter #(.binvalue(6)) binary_to_bcd_converter_1: pin names not known; wires that end beside it: counter_2_q, Hour_tens_t, Hour_ones_t
  // Binary_to_BCD_converter #(.binvalue(6)) binary_to_bcd_converter_2: pin names not known; wires that end beside it: counter_3_q, Minute_tens_t, Minute_ones_t
  Counter #(.max('h7), .width(3)) counter_6 (
    .clr(Counter6_1_output_1), .load(Input_1), .up(Input_2), .count(Input_2), .clk(CLK10k), .Q(counter_6_q));  // open: D, carry
  // Binary_to_BCD_converter #(.binvalue(6)) binary_to_bcd_converter_3: pin names not known; wires that end beside it: counter_4_q, Second_tens_t, Second_ones_t
  Counter100 Counter100_1 (.Input_bus_1(counter_5_q), .Output_1(CLK1));
  Decoder #(.select(3)) decoder_1 (
    .out0(Hour_tens), .out1(Hour_ones), .out2(Minute_tens), .out3(Minute_ones), .out4(Second_tens),
    .out5(Second_ones), .sel(counter_6_q), .en(1'b1));  // open: out6, out7
  Counter6 Counter6_1 (.Input_bus_1(counter_6_q), .Output_1(Counter6_1_output_1));
  Multiplexer #(.select(3), .width(4)) multiplexer_1 (
    .in0(Hour_tens_t), .in1(Hour_ones_t), .in2(Minute_tens_t), .in3(Minute_ones_t), .in4(Second_tens_t),
    .in5(Second_ones_t), .out(multiplexer_1_out), .sel(counter_6_q));  // open: in6, in7
  // Binary_to_BCD_converter #(.binvalue(4)) binary_to_bcd_converter_4: pin names not known; wires that end beside it: multiplexer_1_out, binary_to_bcd_converter_4_p2
  // BCD_to_7_Segment_decoder bcd_to_7_segment_decoder_1: pin names not known; wires that end beside it: binary_to_bcd_converter_4_p2
  _7_Segment_Display #(.decimalPoint("false")) L_7_Segment_DisplayReal (
    .g(G), .f(F), .a(A), .b(B), .e(E), .d(D), .c(C));

  // Other names for the same wires on the sheet: Enable = Input_2; Set = Input_1
endmodule

module Counter6 (
  input  [2:0] Input_bus_1,
  output Output_1
);

  wire not_1_out;

  not not_1 (not_1_out, Input_bus_1[0]);
  and and_1 (Output_1, Input_bus_1[2], Input_bus_1[1], not_1_out);
endmodule

module Counter60 (
  input  [5:0] Input_bus_1,
  output Output_1
);

  wire not_1_out, not_2_out;

  not not_1 (not_1_out, Input_bus_1[1]);
  not not_2 (not_2_out, Input_bus_1[0]);
  and and_1 (Output_1, Input_bus_1[5], Input_bus_1[4], Input_bus_1[3], Input_bus_1[2], not_1_out, not_2_out);
endmodule

module Counter24 (
  input  [5:0] Input_bus_1,
  output Output_1
);

  wire not_1_out, not_2_out, not_3_out, not_4_out;

  not not_1 (not_1_out, Input_bus_1[5]);
  not not_2 (not_2_out, Input_bus_1[2]);
  not not_3 (not_3_out, Input_bus_1[1]);
  not not_4 (not_4_out, Input_bus_1[0]);
  and and_1 (Output_1, not_1_out, Input_bus_1[4], Input_bus_1[3], not_2_out, not_3_out, not_4_out);
endmodule

module Counter10 (
  input  [5:0] A,
  output F
);

  wire not_1_out, not_2_out, not_3_out, not_4_out, not_5_out;

  not not_1 (not_1_out, A[5]);
  not not_2 (not_2_out, A[4]);
  not not_3 (not_3_out, A[3]);
  not not_4 (not_4_out, A[1]);
  not not_5 (not_5_out, A[0]);
  and and_1 (F, not_1_out, not_2_out, not_3_out, A[2], not_4_out, not_5_out);
endmodule

module Counter100 (
  input  [5:0] Input_bus_1,
  output Output_1
);

  wire not_1_out, not_2_out, not_3_out;

  not not_1 (not_1_out, Input_bus_1[3]);
  not not_2 (not_2_out, Input_bus_1[2]);
  not not_3 (not_3_out, Input_bus_1[1]);
  and and_1 (Output_1, Input_bus_1[5], Input_bus_1[4], not_1_out, not_2_out, not_3_out, Input_bus_1[0]);
endmodule

module Counter5 (
  input  [5:0] A,
  output F
);

  wire not_1_out, not_2_out, not_3_out, not_4_out;

  not not_1 (not_1_out, A[5]);
  not not_2 (not_2_out, A[4]);
  not not_3 (not_3_out, A[3]);
  not not_4 (not_4_out, A[1]);
  and and_1 (F, not_1_out, not_2_out, not_3_out, A[2], not_4_out, A[0]);
endmodule

module Counter20 (
  input  [5:0] A,
  output F
);

  wire not_1_out, not_2_out, not_3_out, not_4_out;

  not not_1 (not_1_out, A[5]);
  not not_2 (not_2_out, A[4]);
  not not_3 (not_3_out, A[2]);
  not not_4 (not_4_out, A[0]);
  and and_1 (F, not_1_out, not_2_out, A[3], not_3_out, A[1], not_4_out);
endmodule
